// Logisim project poc_mini.circ as structural Verilog: 55 circuits, main circuit main
module main (
);

  wire button_7_out, clock_1_out, cpu_1_dbg_i, cpu_1_moe, cpu_1_mwe, cpu_1_w16, memif8_16rxm_1_bothoe,
       memif8_16rxm_1_bothwe, memif8_16rxm_1_evene, memif8_16rxm_1_odde, not_1_out;
  wire [3:0] cpu_1_dbg_clk, cpu_1_dbg_pc, cpu_1_dbg_pc_2, cpu_1_dbg_pc_3, cpu_1_dbg_pc_4, cpu_1_dbg_r1,
       cpu_1_dbg_r1_2, cpu_1_dbg_r1_3, cpu_1_dbg_r1_4, cpu_1_dbg_r3, cpu_1_dbg_r3_2, cpu_1_dbg_r3_3,
       cpu_1_dbg_r3_4, cpu_1_dbg_r5, cpu_1_dbg_r5_2, cpu_1_dbg_r5_3, cpu_1_dbg_r5_4, cpu_1_dbg_sel2,
       cpu_1_dbg_sel3, cpu_1_dbg_sel3_2, cpu_1_dbg_sel6, cpu_1_dbg_sel7, cpu_1_dbg_sel7_2;
  wire [5:0] button_6_out;
  wire [7:0] cpu_1_dbg_sel0, cpu_1_dbg_sel1, cpu_1_dbg_sel4, cpu_1_dbg_sel5;
  wire [7:4] cpu_1_dbg_sel2_2, cpu_1_dbg_sel6_2;
  wire [8:0] cpu_1_droma;
  wire [12:0] bit_extender_1_out;
  wire [15:0] cpu_1_dbg_f, cpu_1_dbg_r0, cpu_1_dbg_r2, cpu_1_dbg_r4, cpu_1_dbg_r6, cpu_1_mdo,
       memif8_16rxm_1_do, memif8_16rxm_1_ramdo, ram_1_dout, rom_2_data;
  wire [20:0] memif8_16rxm_1_ao;
  wire [21:0] cpu_1_ma;
  wire [31:0] rom_1_data;

  Clock clock_1 (.out(clock_1_out));
  Button button_1 (.out(button_6_out[5]));
  Button button_2 (.out(button_6_out[4]));
  Button button_3 (.out(button_6_out[3]));
  ROM #(.addrWidth(9), .dataWidth(32)) rom_1 (.addr(cpu_1_droma), .data(rom_1_data));
  Button button_4 (.out(button_6_out[2]));
  Button button_5 (.out(button_6_out[1]));
  Button button_6 (.out(button_6_out[0]));
  Button button_7 (.out(button_7_out));
  MemIf8_16RxM memif8_16rxm_1 (
    .RAMDI(ram_1_dout), .ROMDI(rom_2_data), .AI(cpu_1_ma), .DI(cpu_1_mdo), .OE(cpu_1_moe), .WE(cpu_1_mwe),
    .W16(cpu_1_w16), .AO(memif8_16rxm_1_ao), .RAMDO(memif8_16rxm_1_ramdo), .DO(memif8_16rxm_1_do),
    .BothOE(memif8_16rxm_1_bothoe), .BothWE(memif8_16rxm_1_bothwe), .EvenE(memif8_16rxm_1_evene),
    .OddE(memif8_16rxm_1_odde));
  not not_1 (not_1_out, button_7_out);
  RAM #(.addrWidth(21), .asyncread("true"), .byteenables("byteEnables"), .dataWidth(16)) ram_1 (
    .addr(memif8_16rxm_1_ao), .we(memif8_16rxm_1_bothwe), .oe(memif8_16rxm_1_bothoe), .clk(clock_1_out),
    .din(memif8_16rxm_1_ramdo), .dout(ram_1_dout), .be1(memif8_16rxm_1_odde), .be0(memif8_16rxm_1_evene));
  ROM #(.addrWidth(13), .dataWidth(16)) rom_2 (.addr(bit_extender_1_out), .data(rom_2_data));
  Bit_Extender #(.in_width(21), .out_width(13), .\type ("zero")) bit_extender_1 (
    .in(memif8_16rxm_1_ao), .out(bit_extender_1_out));
  CPU cpu_1 (
    .CLK(clock_1_out), .MDI(memif8_16rxm_1_do), .IRQD(button_6_out), .nRST(not_1_out), .DROMD(rom_1_data),
    .MA(cpu_1_ma), .MDO(cpu_1_mdo), .DBG_F(cpu_1_dbg_f), .DBG_I(cpu_1_dbg_i),
    .DBG_PC({cpu_1_dbg_pc_4, cpu_1_dbg_pc_3, cpu_1_dbg_pc_2, cpu_1_dbg_pc}), .DBG_R0(cpu_1_dbg_r0),
    .DBG_R1({cpu_1_dbg_r1_4, cpu_1_dbg_r1_3, cpu_1_dbg_r1_2, cpu_1_dbg_r1}), .DBG_R2(cpu_1_dbg_r2),
    .DBG_R3({cpu_1_dbg_r3_4, cpu_1_dbg_r3_3, cpu_1_dbg_r3_2, cpu_1_dbg_r3}), .DBG_R4(cpu_1_dbg_r4),
    .DBG_R5({cpu_1_dbg_r5_4, cpu_1_dbg_r5_3, cpu_1_dbg_r5_2, cpu_1_dbg_r5}), .DBG_R6(cpu_1_dbg_r6),
    .DBG_CLK(cpu_1_dbg_clk), .DBG_SEL0(cpu_1_dbg_sel0), .DBG_SEL1(cpu_1_dbg_sel1),
    .DBG_SEL2({cpu_1_dbg_sel2_2, cpu_1_dbg_sel2}), .DBG_SEL3({cpu_1_dbg_sel3_2, cpu_1_dbg_sel3}),
    .DBG_SEL4(cpu_1_dbg_sel4), .DBG_SEL5(cpu_1_dbg_sel5), .DBG_SEL6({cpu_1_dbg_sel6_2, cpu_1_dbg_sel6}),
    .DBG_SEL7({cpu_1_dbg_sel7_2, cpu_1_dbg_sel7}), .DROMA(cpu_1_droma), .MOE(cpu_1_moe), .MWE(cpu_1_mwe),
    .W16(cpu_1_w16));
  Hex_Digit_Display hex_digit_display_1 (.value(cpu_1_dbg_clk));  // open: dp
  LED led_1 (.in(cpu_1_dbg_i));
  Hex_Digit_Display hex_digit_display_2 (.value(cpu_1_dbg_sel0[7:4]));  // open: dp
  Hex_Digit_Display hex_digit_display_3 (.value(cpu_1_dbg_sel4[7:4]));  // open: dp
  Hex_Digit_Display hex_digit_display_4 (.value(cpu_1_dbg_f[15:12]));  // open: dp
  Hex_Digit_Display hex_digit_display_5 (.value(cpu_1_dbg_f[11:8]));  // open: dp
  LED led_2 (.in(cpu_1_dbg_f[15]));
  LED led_3 (.in(cpu_1_dbg_f[14]));
  LED led_4 (.in(cpu_1_dbg_f[13]));
  Hex_Digit_Display hex_digit_display_6 (.value(cpu_1_dbg_r0[15:12]));  // open: dp
  Hex_Digit_Display hex_digit_display_7 (.value(cpu_1_dbg_r0[11:8]));  // open: dp
  Hex_Digit_Display hex_digit_display_8 (.value(cpu_1_dbg_r2[15:12]));  // open: dp
  Hex_Digit_Display hex_digit_display_9 (.value(cpu_1_dbg_r2[11:8]));  // open: dp
  Hex_Digit_Display hex_digit_display_10 (.value(cpu_1_dbg_r4[15:12]));  // open: dp
  Hex_Digit_Display hex_digit_display_11 (.value(cpu_1_dbg_r4[11:8]));  // open: dp
  Hex_Digit_Display hex_digit_display_12 (.value(cpu_1_dbg_r6[15:12]));  // open: dp
  Hex_Digit_Display hex_digit_display_13 (.value(cpu_1_dbg_r6[11:8]));  // open: dp
  Hex_Digit_Display hex_digit_display_14 (.value(cpu_1_dbg_sel0[3:0]));  // open: dp
  Hex_Digit_Display hex_digit_display_15 (.value(cpu_1_dbg_sel1[7:4]));  // open: dp
  Hex_Digit_Display hex_digit_display_16 (.value(cpu_1_dbg_sel4[3:0]));  // open: dp
  Hex_Digit_Display hex_digit_display_17 (.value(cpu_1_dbg_sel5[7:4]));  // open: dp
  Hex_Digit_Display hex_digit_display_18 (.value(cpu_1_dbg_f[7:4]));  // open: dp
  Hex_Digit_Display hex_digit_display_19 (.value(cpu_1_dbg_f[3:0]));  // open: dp
  LED led_5 (.in(cpu_1_dbg_f[12]));
  LED led_6 (.in(cpu_1_dbg_f[11]));
  LED led_7 (.in(cpu_1_dbg_f[10]));
  LED led_8 (.in(cpu_1_dbg_f[9]));
  Hex_Digit_Display hex_digit_display_20 (.value(cpu_1_dbg_r0[7:4]));  // open: dp
  Hex_Digit_Display hex_digit_display_21 (.value(cpu_1_dbg_r0[3:0]));  // open: dp
  Hex_Digit_Display hex_digit_display_22 (.value(cpu_1_dbg_r2[7:4]));  // open: dp
  Hex_Digit_Display hex_digit_display_23 (.value(cpu_1_dbg_r2[3:0]));  // open: dp
  Hex_Digit_Display hex_digit_display_24 (.value(cpu_1_dbg_r4[7:4]));  // open: dp
  Hex_Digit_Display hex_digit_display_25 (.value(cpu_1_dbg_r4[3:0]));  // open: dp
  Hex_Digit_Display hex_digit_display_26 (.value(cpu_1_dbg_r6[7:4]));  // open: dp
  Hex_Digit_Display hex_digit_display_27 (.value(cpu_1_dbg_r6[3:0]));  // open: dp
  Hex_Digit_Display hex_digit_display_28 (.value(cpu_1_dbg_sel1[3:0]));  // open: dp
  Hex_Digit_Display hex_digit_display_29 (.value(cpu_1_dbg_sel5[3:0]));  // open: dp
  LED led_9 (.in(cpu_1_dbg_f[6]));
  LED led_10 (.in(cpu_1_dbg_f[5]));
  LED led_11 (.in(cpu_1_dbg_f[8]));
  LED led_12 (.in(cpu_1_dbg_f[7]));
  Hex_Digit_Display hex_digit_display_30 (.value(cpu_1_dbg_r1_4));  // open: dp
  Hex_Digit_Display hex_digit_display_31 (.value(cpu_1_dbg_r3_4));  // open: dp
  Hex_Digit_Display hex_digit_display_32 (.value(cpu_1_dbg_r5_4));  // open: dp
  Hex_Digit_Display hex_digit_display_33 (.value(cpu_1_dbg_pc_4));  // open: dp
  Hex_Digit_Display hex_digit_display_34 (.value(cpu_1_dbg_sel2));  // open: dp
  Hex_Digit_Display hex_digit_display_35 (.value(cpu_1_dbg_sel2_2));  // open: dp
  Hex_Digit_Display hex_digit_display_36 (.value(cpu_1_dbg_sel6));  // open: dp
  Hex_Digit_Display hex_digit_display_37 (.value(cpu_1_dbg_sel6_2));  // open: dp
  LED led_13 (.in(cpu_1_dbg_f[3]));
  LED led_14 (.in(cpu_1_dbg_f[2]));
  LED led_15 (.in(cpu_1_dbg_f[1]));
  LED led_16 (.in(cpu_1_dbg_f[4]));
  Hex_Digit_Display hex_digit_display_38 (.value(cpu_1_dbg_r1_3));  // open: dp
  Hex_Digit_Display hex_digit_display_39 (.value(cpu_1_dbg_r1_2));  // open: dp
  Hex_Digit_Display hex_digit_display_40 (.value(cpu_1_dbg_r3_3));  // open: dp
  Hex_Digit_Display hex_digit_display_41 (.value(cpu_1_dbg_r3_2));  // open: dp
  Hex_Digit_Display hex_digit_display_42 (.value(cpu_1_dbg_r5_3));  // open: dp
  Hex_Digit_Display hex_digit_display_43 (.value(cpu_1_dbg_r5_2));  // open: dp
  Hex_Digit_Display hex_digit_display_44 (.value(cpu_1_dbg_pc_3));  // open: dp
  Hex_Digit_Display hex_digit_display_45 (.value(cpu_1_dbg_pc_2));  // open: dp
  Hex_Digit_Display hex_digit_display_46 (.value(cpu_1_dbg_sel3_2));  // open: dp
  Hex_Digit_Display hex_digit_display_47 (.value(cpu_1_dbg_sel3));  // open: dp
  Hex_Digit_Display hex_digit_display_48 (.value(cpu_1_dbg_sel7_2));  // open: dp
  Hex_Digit_Display hex_digit_display_49 (.value(cpu_1_dbg_sel7));  // open: dp
  LED led_17 (.in(cpu_1_dbg_f[0]));
  Hex_Digit_Display hex_digit_display_50 (.value(cpu_1_dbg_r1));  // open: dp
  Hex_Digit_Display hex_digit_display_51 (.value(cpu_1_dbg_r3));  // open: dp
  Hex_Digit_Display hex_digit_display_52 (.value(cpu_1_dbg_r5));  // open: dp
  Hex_Digit_Display hex_digit_display_53 (.value(cpu_1_dbg_pc));  // open: dp

  // Notes on the sheet:
  //   contents of rom_1 (hex, n*v repeats v):
  //   12*a0028098 8051909e 8051909e 8051909f 8051909f 16*e0028098 12*900a0098 80519097 80519097 80421099
  //   80421099 14*d00a0098 58920008 58920008 12*80528098 80128098 509700f8 80128098 ad798 88158008
  //   80548088 88158008 80548088 88158008 80548088 88158008 80548088 88158008 80548088 88158008 80548088
  //   11e0e8 80148088 600290e8 8015f0f8 801480f8 50aaa8 801480f8 8850aac8 801480f8 850aac8 801480f8 50bcb9
  //   801480f8 845020ae 801480f8 8020a0ae 4*ed7f8 16*8017f0f8 14*8013f0f8 8010888c 80108087 80508980
  //   80508981 80508982 80508983 80508984 80508987 8050898e 8050898f 8050898a 8050898b 80508988 80508989
  //   80500989 88108908 8208009e 8600809e 500f00e8 15*80518084 e180f008 15*80518080 14*8013f0f8 8010888d
  //   88508809 8850880a 15*10091 17e0e9 15*80518083 e00089f8 9f8 14*80518081 62*8017f0f8 8017e0e8 8017e0e8
  //   13*8017f0f8 8912f008 8017f0f8 8010f00e 12*8017f0f8 8010f0de 8017f0f8 d0d00098 8017f0f8 8017f0f8
  //   8050bbba 8017f0f8 8017f0f8 8017f0f8 8850bb0a 8017f0f8 8850bbc8 4*8017f0f8 4*8010f00e 48*8017f0f8
  //   8017e0e8 48*8017f0f8 15*80508808 e00780e8 16*8017f0f8 d090008e 14*8017f0f8
  //   IRQ5...0
  //   RESET
  //   contents of rom_2 (hex, n*v repeats v):
  //   3f80 17a d847 d84d d852 d85c d8aa d8b0 23*ffb0 9b70 770c 730a 6f08 6b06 6704 6302 d7ff 6b00 e51d
  //   ace0 ac0f e11d e3ba e3f4 e816 ffc1 e11d ebcf e116 e89d e997 e815 d3ff e997 f01d f3f6 927f ea16 d3ff
  //   9b87 9b85 2b00 e997 d3ff 2302 2704 2b06 2f08 330a 370c 9b10 ffb0 977e 2280 8402 1c81 5881 6680 ffb0
  //   977e 2280 8402 1c81 6680 ffb0 9b7e f41d f7be e041 e69e 3700 1a81 f417 7700 9b02 ffb0 9b6c 7310 6f0e
  //   6b0c 670a 6308 3712 9682 7712 1a81 e0c1 9b87 2308 270a b402 f29f 7306 ee9e b400 b681 f71c b40a e040
  //   b40e f29f 7704 7302 e69e e3f2 e3b2 e2de ebf2 ebb2 a901 3310 1a03 e281 897e eb9b e570 6400 8902 8002
  //   927f fe89 eb9a 8974 3310 f3b2 e3c1 7300 897e eb9b e570 ed70 f170 f570 6400 6c02 7004 7406 8908 8008
  //   bc80 fd09 3704 3302 f29e b402 3306 f29e 9b85 2308 270a 2b0c 2f0e 3310 9b14 ffb0 a042 a10d 977e 2680
  //   8482 6680 ffb0 9b7e 6b00 d7ff 9b02 ffb0 a800 d3ff ffc6 ffc2 ffc1 ffc0 ffc3 ffc4 ffc5 a802 d3ff ffc6
  //   ffc2 ffc1 ffc8 ffcb ffc4 ffc5 a804 d3ff ffc6 ffc2 ffc9 ffc0 ffcb ffc4 ffcd a806 d3ff ffc6 ffc2 ffc9
  //   ffc8 ffcb ffc4 ffcd a808 d3ff ffc6 ffca ffc1 ffc0 ffc3 ffcc ffcd a80a d3ff ffc6 ffca ffc1 ffc8 ffcb
  //   ffcc ffcd a80c d3ff ffc6 ffca ffc9 ffc0 ffcb ffcc ffcd a80e d3ff ffc6 ffca ffc9 ffc8 ffcb ffcc ffcd
  //   a810 d3ff ffc7 ffc2 ffc1 ffc0 ffc3 ffcc ffcd a812 d3ff ffc7 ffc2 ffc1 ffc8 ffcb ffcc ffcd a814 d3ff
  //   ffc7 ffc2 ffc9 ffc0 ffcb ffcc ffcd a816 d3ff ffc7 ffc2 ffc9 ffc8 ffcb ffcc ffcd a818 d3ff ffc7 ffca
  //   ffc1 ffc0 ffc3 ffc4 ffc5 a81a d3ff ffc7 ffca ffc1 ffc8 ffcb ffc4 ffc5 a81c d3ff ffc7 ffca ffc9 ffc0
  //   ffcb ffc4 ffcd a81e d3ff ffc7 ffca ffc9 ffc8 ffcb ffc4 ffcd e01c ffc0 5fff ffc8 a406 a842 e49c ffc9
  //   e91c ffc9 e51c ffc1 e89c ffc1 a380 803f 8001 ffc9 a782 84bf ffc9 abfe 8901 ffc9 ac00 8d80 ffc9 b002
  //   927f ffc9 b47e 96c1 ffc9 a000 8000 a001 ffc9 a000 a001 a422 84ef a401 ffc9 a422 a401 a844 895e a801
  //   ffc9 a844 a801 ae66 8dcd ac05 ffc9 ac66 affd b288 923c b003 ffc9 b088 b3fd b6aa 96ab b403 ffc9 b4aa
  //   b7fd a0dc a3bb 8012 a045 ffc9 a0dc a3bb a498 a733 84b4 a4cd ffc9 a498 a733 a854 aaab 8956 a957 ffc9
  //   a854 aaab ac10 ae23 8df8 addf ffc9 ac10 ae23 b0cc b199 921a b267 ffc9 b0cc b199 b488 b511 96bc b6ef
  //   ffc9 b488 b511 a022 a045 806f a3bd ffc9 a022 a045 a466 a4cd 84cd a735 ffc9 a466 a4cd a8aa a955 892b
  //   aaab ffc9 a8aa a955 acee addd 8d89 ae23 ffc9 acee addd b032 b267 9267 b19b ffc9 b032 b267 b476 b6ef
  //   96c5 b513 ffc9 b476 b6ef a022 a045 a466 a4cd a8aa a955 acee addd b032 b267 b476 b6ef e09d 804d a335
  //   ffc9 a066 a0cd f41d 96cd b735 ffc9 b466 b4cd e61d 84e7 a59b ffc9 a432 a667 e99d 8909 aa23 ffc9 a8ee
  //   a9dd ee1d 8de7 ad9b ffc9 ac32 ae67 f01d 924d b335 ffc9 b066 b0cd a022 e01c e088 8001 8002 8004 806b
  //   a001 ffc9 a02a a001 5fff e088 8001 8002 8004 8064 a001 ffc9 a038 a001 e01c e080 8001 8002 8004 805d
  //   a001 ffc9 a046 a001 5fff e080 8001 8002 8004 8059 a001 ffc9 a04e a001 5fff e080 8008 e01c ff40 8051
  //   a001 ffc9 a05e a001 a054 bc09 8001 8002 8004 8052 a001 ffc9 a05c a001 8008 bc01 804a a001 ffc9 a06c
  //   a001 bc09 8010 bc05 bff5 803a a3ff ffc9 a08c a001 a054 8f82 d802 8001 8002 8004 8052 a001 ffc9 a05c
  //   a001 f59c ffc9 8f8c d804 8010 f59c ffc9 d801 dffb 8042 a001 ffc9 a07c a001 a7fe a954 ac66 adf1 f19d
  //   18d5 ffc1 84ab a7ff ffc9 a4aa a401 1955 ffc9 8900 a801 ffc9 a800 a801 1dc5 ffc1 8d89 ae0f ffc9 acee
  //   adf1 5a7a ffc1 9237 b20f ffc9 b092 b1f1 a7fe b000 e61f 8480 a401 ffc9 a400 a401 abfe ac08 e99f 8900
  //   a801 ffc9 a800 a801 a4aa a802 e51e ed1f 8dab afff ffc9 acaa ac01 ad54 b004 ee1e f61f 96d6 b7ff ffc9
  //   b454 b403 b586 a006 f41e e41f 84bd a7fd ffc9 a486 a403 a478 a00a e41e f41f 96c4 b401 ffc9 b478 b401
  //   ade0 a80c ed1e e51f 8490 a7fd ffc9 a4e0 a403 b41e b00e f61e ee1f 8df1 ac01 ffc9 ac1e ac01 a002 a408
  //   e09e a000 a041 9800 e31d 8000 a3c1 ffc9 a000 a041 9b7e a068 a049 6300 2700 84cc a7b9 ffc9 a468 a449
  //   a096 a3b7 6300 2700 84b5 a449 ffc9 a496 a7b7 9b02 a800 d3ff 9b8d 805f a2f5 ffc9 a042 a10d 1881 ffc9
  //   9b87 9b8d 805f a2f5 ffc9 a042 a10d 1881 ffc1 9b87 9b8d 1881 ffc1 9b85 9b8d 1881 ffc9 9b87 9b8d 1881
  //   ffc1 9b85 9b8d 1881 ffc9 9b85 9b8d 1881 ffc9 9b87 9b8d 1881 ffc1 9b87 9b8d 1881 ffc1 9b87 9b8d 1881
  //   ffc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
  //   Ints Enabled
  //   SEL0
  //   SEL4
  //   IRQ5...0 Mask
  //   Flags
  //   R0
  //   R2
  //   R4
  //   SP
  //   SEL1
  //   SEL5
  //   IRQ5...0 Requested
  //   SEL2
  //   SEL6
  //   O
  //   S
  //   Z
  //   R1
  //   R3
  //   R5
  //   PC
  //   SEL3
  //   SEL7
  //   C
endmodule

module PlayGround (
);

  wire adder16_1_co, adder16_1_ovf, alu_1_co, alu_1_ovf, alu_1_s, alu_1_z, alu_2_co, alu_2_ovf, alu_2_s,
       alu_2_z, button_1_out, button_2_out, button_3_out, clock_1_out, condeval_1_condval,
       condeval_2_condval, dipswitch_18_sw1, dipswitch_18_sw2, dipswitch_19_sw1, dipswitch_19_sw2,
       dipswitch_20_sw1, dipswitch_20_sw3, dipswitch_20_sw4, dipswitch_23_sw1, dipswitch_23_sw2,
       dipswitch_23_sw3, dipswitch_23_sw4, dipswitch_27_sw1, dipswitch_27_sw2, dipswitch_27_sw3,
       dipswitch_30_sw1, dipswitch_30_sw2, dipswitch_30_sw3, dipswitch_30_sw4, dipswitch_34_sw2,
       dipswitch_35_sw2, dipswitch_36_sw1, dipswitch_36_sw2, dipswitch_36_sw3, dipswitch_37_sw1,
       dipswitch_37_sw2, dipswitch_38_sw1, dipswitch_38_sw2, dipswitch_39_sw2, dipswitch_42_sw1,
       dipswitch_42_sw2, dipswitch_42_sw3, dipswitch_44_sw2, dipswitch_47_sw1, dipswitch_47_sw2,
       dipswitch_47_sw3, dipswitch_47_sw4, dipswitch_48_sw1, dipswitch_48_sw2, memif8_16w_1_bothoe,
       memif8_16w_1_bothwe, memif8_16w_1_evene, memif8_16w_1_odde, n74138_1_pin4, n74138_1_pin6,
       n74138_1_pin10, n74138_1_pin11, n74138_1_pin12, n74138_1_pin14, n74138_1_pin15, not_1_out, not_2_out,
       not_3_out, not_4_out, not_5_out, not_6_out, not_7_out, not_8_out, not_9_out, not_10_out,
       ramprot_1_oeo, ramprot_1_weo, register_1_q, register_2_q, register_3_q, register_4_q, register_5_q,
       sel1of8_1_do, undriven;
  wire [2:0] dipswitch_28_sw3, dipswitch_31_sw3, dipswitch_32_sw3, dipswitch_33_sw3, dipswitch_40_sw3,
       dipswitch_45_sw3, dipswitch_46_sw3;
  wire [3:0] conddecoder_1_condcode, dipswitch_29_sw4, dipswitch_41_sw4;
  wire [7:0] dipswitch_14_sw8, dipswitch_26_sw16, instrcompressor_1_instro, regcnt8_1_q;
  wire [15:0] adder16_1_do, alu_1_do, bitrev16_1_do, buf16_1_do, buf16_2_do, dipswitch_1_sw16,
       dipswitch_2_sw16, dipswitch_3_sw16, dipswitch_4_sw16, dipswitch_5_sw16, dipswitch_6_sw16,
       dipswitch_7_sw16, dipswitch_8_sw16, dipswitch_9_sw16, dipswitch_10_sw16, dipswitch_11_sw16,
       dipswitch_12_sw16, dipswitch_13_sw16, dipswitch_15_sw16, dipswitch_16_sw16, dipswitch_21_sw16,
       dipswitch_22_sw16, dipswitch_24_sw16, dipswitch_25_sw16, dipswitch_43_sw16, immdecoder_1_imm,
       memif8_16w_1_do, memif8_16w_1_mdo, ram8_16_1_do, ram8_16_2_do, ram_1_dout, reg16buf_1_q,
       regfileold_1_q0, regfileold_1_q1, regfileold_1_qpc, regfileold_2_qpc, regpc_1_q, regpc_1_qpc,
       shifter16_1_do;
  wire [15:8] dipswitch_26_sw8;
  wire [20:0] memif8_16w_1_ao;
  wire [21:0] dipswitch_17_sw22;
  wire [23:0] bit_extender_1_out;

  Clock clock_1 (.out(clock_1_out));
  DipSwitch #(.number(16)) dipswitch_1 (
    .sw1(dipswitch_1_sw16[15]), .sw2(dipswitch_1_sw16[14]), .sw3(dipswitch_1_sw16[13]),
    .sw4(dipswitch_1_sw16[12]), .sw5(dipswitch_1_sw16[11]), .sw6(dipswitch_1_sw16[10]),
    .sw7(dipswitch_1_sw16[9]), .sw8(dipswitch_1_sw16[8]), .sw9(dipswitch_1_sw16[7]),
    .sw10(dipswitch_1_sw16[6]), .sw11(dipswitch_1_sw16[5]), .sw12(dipswitch_1_sw16[4]),
    .sw13(dipswitch_1_sw16[3]), .sw14(dipswitch_1_sw16[2]), .sw15(dipswitch_1_sw16[1]),
    .sw16(dipswitch_1_sw16[0]));
  DipSwitch #(.number(16)) dipswitch_2 (
    .sw1(dipswitch_2_sw16[15]), .sw2(dipswitch_2_sw16[14]), .sw3(dipswitch_2_sw16[13]),
    .sw4(dipswitch_2_sw16[12]), .sw5(dipswitch_2_sw16[11]), .sw6(dipswitch_2_sw16[10]),
    .sw7(dipswitch_2_sw16[9]), .sw8(dipswitch_2_sw16[8]), .sw9(dipswitch_2_sw16[7]),
    .sw10(dipswitch_2_sw16[6]), .sw11(dipswitch_2_sw16[5]), .sw12(dipswitch_2_sw16[4]),
    .sw13(dipswitch_2_sw16[3]), .sw14(dipswitch_2_sw16[2]), .sw15(dipswitch_2_sw16[1]),
    .sw16(dipswitch_2_sw16[0]));
  DipSwitch #(.number(16)) dipswitch_3 (
    .sw1(dipswitch_3_sw16[15]), .sw2(dipswitch_3_sw16[14]), .sw3(dipswitch_3_sw16[13]),
    .sw4(dipswitch_3_sw16[12]), .sw5(dipswitch_3_sw16[11]), .sw6(dipswitch_3_sw16[10]),
    .sw7(dipswitch_3_sw16[9]), .sw8(dipswitch_3_sw16[8]), .sw9(dipswitch_3_sw16[7]),
    .sw10(dipswitch_3_sw16[6]), .sw11(dipswitch_3_sw16[5]), .sw12(dipswitch_3_sw16[4]),
    .sw13(dipswitch_3_sw16[3]), .sw14(dipswitch_3_sw16[2]), .sw15(dipswitch_3_sw16[1]),
    .sw16(dipswitch_3_sw16[0]));
  DipSwitch #(.number(16)) dipswitch_4 (
    .sw1(dipswitch_4_sw16[15]), .sw2(dipswitch_4_sw16[14]), .sw3(dipswitch_4_sw16[13]),
    .sw4(dipswitch_4_sw16[12]), .sw5(dipswitch_4_sw16[11]), .sw6(dipswitch_4_sw16[10]),
    .sw7(dipswitch_4_sw16[9]), .sw8(dipswitch_4_sw16[8]), .sw9(dipswitch_4_sw16[7]),
    .sw10(dipswitch_4_sw16[6]), .sw11(dipswitch_4_sw16[5]), .sw12(dipswitch_4_sw16[4]),
    .sw13(dipswitch_4_sw16[3]), .sw14(dipswitch_4_sw16[2]), .sw15(dipswitch_4_sw16[1]),
    .sw16(dipswitch_4_sw16[0]));
  DipSwitch #(.number(16)) dipswitch_5 (
    .sw1(dipswitch_5_sw16[15]), .sw2(dipswitch_5_sw16[14]), .sw3(dipswitch_5_sw16[13]),
    .sw4(dipswitch_5_sw16[12]), .sw5(dipswitch_5_sw16[11]), .sw6(dipswitch_5_sw16[10]),
    .sw7(dipswitch_5_sw16[9]), .sw8(dipswitch_5_sw16[8]), .sw9(dipswitch_5_sw16[7]),
    .sw10(dipswitch_5_sw16[6]), .sw11(dipswitch_5_sw16[5]), .sw12(dipswitch_5_sw16[4]),
    .sw13(dipswitch_5_sw16[3]), .sw14(dipswitch_5_sw16[2]), .sw15(dipswitch_5_sw16[1]),
    .sw16(dipswitch_5_sw16[0]));
  DipSwitch #(.number(16)) dipswitch_6 (
    .sw1(dipswitch_6_sw16[15]), .sw2(dipswitch_6_sw16[14]), .sw3(dipswitch_6_sw16[13]),
    .sw4(dipswitch_6_sw16[12]), .sw5(dipswitch_6_sw16[11]), .sw6(dipswitch_6_sw16[10]),
    .sw7(dipswitch_6_sw16[9]), .sw8(dipswitch_6_sw16[8]), .sw9(dipswitch_6_sw16[7]),
    .sw10(dipswitch_6_sw16[6]), .sw11(dipswitch_6_sw16[5]), .sw12(dipswitch_6_sw16[4]),
    .sw13(dipswitch_6_sw16[3]), .sw14(dipswitch_6_sw16[2]), .sw15(dipswitch_6_sw16[1]),
    .sw16(dipswitch_6_sw16[0]));
  DipSwitch #(.number(16)) dipswitch_7 (
    .sw1(dipswitch_7_sw16[15]), .sw2(dipswitch_7_sw16[14]), .sw3(dipswitch_7_sw16[13]),
    .sw4(dipswitch_7_sw16[12]), .sw5(dipswitch_7_sw16[11]), .sw6(dipswitch_7_sw16[10]),
    .sw7(dipswitch_7_sw16[9]), .sw8(dipswitch_7_sw16[8]), .sw9(dipswitch_7_sw16[7]),
    .sw10(dipswitch_7_sw16[6]), .sw11(dipswitch_7_sw16[5]), .sw12(dipswitch_7_sw16[4]),
    .sw13(dipswitch_7_sw16[3]), .sw14(dipswitch_7_sw16[2]), .sw15(dipswitch_7_sw16[1]),
    .sw16(dipswitch_7_sw16[0]));
  DipSwitch #(.number(16)) dipswitch_8 (
    .sw1(dipswitch_8_sw16[15]), .sw2(dipswitch_8_sw16[14]), .sw3(dipswitch_8_sw16[13]),
    .sw4(dipswitch_8_sw16[12]), .sw5(dipswitch_8_sw16[11]), .sw6(dipswitch_8_sw16[10]),
    .sw7(dipswitch_8_sw16[9]), .sw8(dipswitch_8_sw16[8]), .sw9(dipswitch_8_sw16[7]),
    .sw10(dipswitch_8_sw16[6]), .sw11(dipswitch_8_sw16[5]), .sw12(dipswitch_8_sw16[4]),
    .sw13(dipswitch_8_sw16[3]), .sw14(dipswitch_8_sw16[2]), .sw15(dipswitch_8_sw16[1]),
    .sw16(dipswitch_8_sw16[0]));
  DipSwitch #(.number(16)) dipswitch_9 (
    .sw1(dipswitch_9_sw16[15]), .sw2(dipswitch_9_sw16[14]), .sw3(dipswitch_9_sw16[13]),
    .sw4(dipswitch_9_sw16[12]), .sw5(dipswitch_9_sw16[11]), .sw6(dipswitch_9_sw16[10]),
    .sw7(dipswitch_9_sw16[9]), .sw8(dipswitch_9_sw16[8]), .sw9(dipswitch_9_sw16[7]),
    .sw10(dipswitch_9_sw16[6]), .sw11(dipswitch_9_sw16[5]), .sw12(dipswitch_9_sw16[4]),
    .sw13(dipswitch_9_sw16[3]), .sw14(dipswitch_9_sw16[2]), .sw15(dipswitch_9_sw16[1]),
    .sw16(dipswitch_9_sw16[0]));
  DipSwitch #(.number(16)) dipswitch_10 (
    .sw1(dipswitch_10_sw16[15]), .sw2(dipswitch_10_sw16[14]), .sw3(dipswitch_10_sw16[13]),
    .sw4(dipswitch_10_sw16[12]), .sw5(dipswitch_10_sw16[11]), .sw6(dipswitch_10_sw16[10]),
    .sw7(dipswitch_10_sw16[9]), .sw8(dipswitch_10_sw16[8]), .sw9(dipswitch_10_sw16[7]),
    .sw10(dipswitch_10_sw16[6]), .sw11(dipswitch_10_sw16[5]), .sw12(dipswitch_10_sw16[4]),
    .sw13(dipswitch_10_sw16[3]), .sw14(dipswitch_10_sw16[2]), .sw15(dipswitch_10_sw16[1]),
    .sw16(dipswitch_10_sw16[0]));
  DipSwitch #(.number(16)) dipswitch_11 (
    .sw1(dipswitch_11_sw16[15]), .sw2(dipswitch_11_sw16[14]), .sw3(dipswitch_11_sw16[13]),
    .sw4(dipswitch_11_sw16[12]), .sw5(dipswitch_11_sw16[11]), .sw6(dipswitch_11_sw16[10]),
    .sw7(dipswitch_11_sw16[9]), .sw8(dipswitch_11_sw16[8]), .sw9(dipswitch_11_sw16[7]),
    .sw10(dipswitch_11_sw16[6]), .sw11(dipswitch_11_sw16[5]), .sw12(dipswitch_11_sw16[4]),
    .sw13(dipswitch_11_sw16[3]), .sw14(dipswitch_11_sw16[2]), .sw15(dipswitch_11_sw16[1]),
    .sw16(dipswitch_11_sw16[0]));
  DipSwitch #(.number(16)) dipswitch_12 (
    .sw1(dipswitch_12_sw16[15]), .sw2(dipswitch_12_sw16[14]), .sw3(dipswitch_12_sw16[13]),
    .sw4(dipswitch_12_sw16[12]), .sw5(dipswitch_12_sw16[11]), .sw6(dipswitch_12_sw16[10]),
    .sw7(dipswitch_12_sw16[9]), .sw8(dipswitch_12_sw16[8]), .sw9(dipswitch_12_sw16[7]),
    .sw10(dipswitch_12_sw16[6]), .sw11(dipswitch_12_sw16[5]), .sw12(dipswitch_12_sw16[4]),
    .sw13(dipswitch_12_sw16[3]), .sw14(dipswitch_12_sw16[2]), .sw15(dipswitch_12_sw16[1]),
    .sw16(dipswitch_12_sw16[0]));
  DipSwitch #(.number(16)) dipswitch_13 (
    .sw1(dipswitch_13_sw16[15]), .sw2(dipswitch_13_sw16[14]), .sw3(dipswitch_13_sw16[13]),
    .sw4(dipswitch_13_sw16[12]), .sw5(dipswitch_13_sw16[11]), .sw6(dipswitch_13_sw16[10]),
    .sw7(dipswitch_13_sw16[9]), .sw8(dipswitch_13_sw16[8]), .sw9(dipswitch_13_sw16[7]),
    .sw10(dipswitch_13_sw16[6]), .sw11(dipswitch_13_sw16[5]), .sw12(dipswitch_13_sw16[4]),
    .sw13(dipswitch_13_sw16[3]), .sw14(dipswitch_13_sw16[2]), .sw15(dipswitch_13_sw16[1]),
    .sw16(dipswitch_13_sw16[0]));
  DipSwitch dipswitch_14 (
    .sw1(dipswitch_14_sw8[7]), .sw2(dipswitch_14_sw8[6]), .sw3(dipswitch_14_sw8[5]),
    .sw4(dipswitch_14_sw8[4]), .sw5(dipswitch_14_sw8[3]), .sw6(dipswitch_14_sw8[2]),
    .sw7(dipswitch_14_sw8[1]), .sw8(dipswitch_14_sw8[0]));
  DipSwitch #(.number(16)) dipswitch_15 (
    .sw1(dipswitch_15_sw16[15]), .sw2(dipswitch_15_sw16[14]), .sw3(dipswitch_15_sw16[13]),
    .sw4(dipswitch_15_sw16[12]), .sw5(dipswitch_15_sw16[11]), .sw6(dipswitch_15_sw16[10]),
    .sw7(dipswitch_15_sw16[9]), .sw8(dipswitch_15_sw16[8]), .sw9(dipswitch_15_sw16[7]),
    .sw10(dipswitch_15_sw16[6]), .sw11(dipswitch_15_sw16[5]), .sw12(dipswitch_15_sw16[4]),
    .sw13(dipswitch_15_sw16[3]), .sw14(dipswitch_15_sw16[2]), .sw15(dipswitch_15_sw16[1]),
    .sw16(dipswitch_15_sw16[0]));
  DipSwitch #(.number(16)) dipswitch_16 (
    .sw1(dipswitch_16_sw16[15]), .sw2(dipswitch_16_sw16[14]), .sw3(dipswitch_16_sw16[13]),
    .sw4(dipswitch_16_sw16[12]), .sw5(dipswitch_16_sw16[11]), .sw6(dipswitch_16_sw16[10]),
    .sw7(dipswitch_16_sw16[9]), .sw8(dipswitch_16_sw16[8]), .sw9(dipswitch_16_sw16[7]),
    .sw10(dipswitch_16_sw16[6]), .sw11(dipswitch_16_sw16[5]), .sw12(dipswitch_16_sw16[4]),
    .sw13(dipswitch_16_sw16[3]), .sw14(dipswitch_16_sw16[2]), .sw15(dipswitch_16_sw16[1]),
    .sw16(dipswitch_16_sw16[0]));
  DipSwitch #(.number(22)) dipswitch_17 (
    .sw1(dipswitch_17_sw22[21]), .sw2(dipswitch_17_sw22[20]), .sw3(dipswitch_17_sw22[19]),
    .sw4(dipswitch_17_sw22[18]), .sw5(dipswitch_17_sw22[17]), .sw6(dipswitch_17_sw22[16]),
    .sw7(dipswitch_17_sw22[15]), .sw8(dipswitch_17_sw22[14]), .sw9(dipswitch_17_sw22[13]),
    .sw10(dipswitch_17_sw22[12]), .sw11(dipswitch_17_sw22[11]), .sw12(dipswitch_17_sw22[10]),
    .sw13(dipswitch_17_sw22[9]), .sw14(dipswitch_17_sw22[8]), .sw15(dipswitch_17_sw22[7]),
    .sw16(dipswitch_17_sw22[6]), .sw17(dipswitch_17_sw22[5]), .sw18(dipswitch_17_sw22[4]),
    .sw19(dipswitch_17_sw22[3]), .sw20(dipswitch_17_sw22[2]), .sw21(dipswitch_17_sw22[1]),
    .sw22(dipswitch_17_sw22[0]));
  DipSwitch #(.number(2)) dipswitch_18 (.sw1(dipswitch_18_sw1), .sw2(dipswitch_18_sw2));
  DipSwitch #(.number(2)) dipswitch_19 (.sw1(dipswitch_19_sw1), .sw2(dipswitch_19_sw2));
  DipSwitch #(.number(4)) dipswitch_20 (
    .sw1(dipswitch_20_sw1), .sw3(dipswitch_20_sw3), .sw4(dipswitch_20_sw4));  // open: sw2
  DipSwitch #(.number(16)) dipswitch_21 (
    .sw1(dipswitch_21_sw16[15]), .sw2(dipswitch_21_sw16[14]), .sw3(dipswitch_21_sw16[13]),
    .sw4(dipswitch_21_sw16[12]), .sw5(dipswitch_21_sw16[11]), .sw6(dipswitch_21_sw16[10]),
    .sw7(dipswitch_21_sw16[9]), .sw8(dipswitch_21_sw16[8]), .sw9(dipswitch_21_sw16[7]),
    .sw10(dipswitch_21_sw16[6]), .sw11(dipswitch_21_sw16[5]), .sw12(dipswitch_21_sw16[4]),
    .sw13(dipswitch_21_sw16[3]), .sw14(dipswitch_21_sw16[2]), .sw15(dipswitch_21_sw16[1]),
    .sw16(dipswitch_21_sw16[0]));
  DipSwitch #(.number(16)) dipswitch_22 (
    .sw1(dipswitch_22_sw16[15]), .sw2(dipswitch_22_sw16[14]), .sw3(dipswitch_22_sw16[13]),
    .sw4(dipswitch_22_sw16[12]), .sw5(dipswitch_22_sw16[11]), .sw6(dipswitch_22_sw16[10]),
    .sw7(dipswitch_22_sw16[9]), .sw8(dipswitch_22_sw16[8]), .sw9(dipswitch_22_sw16[7]),
    .sw10(dipswitch_22_sw16[6]), .sw11(dipswitch_22_sw16[5]), .sw12(dipswitch_22_sw16[4]),
    .sw13(dipswitch_22_sw16[3]), .sw14(dipswitch_22_sw16[2]), .sw15(dipswitch_22_sw16[1]),
    .sw16(dipswitch_22_sw16[0]));
  DipSwitch #(.number(4)) dipswitch_23 (
    .sw1(dipswitch_23_sw1), .sw2(dipswitch_23_sw2), .sw3(dipswitch_23_sw3), .sw4(dipswitch_23_sw4));
  DipSwitch #(.number(16)) dipswitch_24 (
    .sw1(dipswitch_24_sw16[15]), .sw2(dipswitch_24_sw16[14]), .sw3(dipswitch_24_sw16[13]),
    .sw4(dipswitch_24_sw16[12]), .sw5(dipswitch_24_sw16[11]), .sw6(dipswitch_24_sw16[10]),
    .sw7(dipswitch_24_sw16[9]), .sw8(dipswitch_24_sw16[8]), .sw9(dipswitch_24_sw16[7]),
    .sw10(dipswitch_24_sw16[6]), .sw11(dipswitch_24_sw16[5]), .sw12(dipswitch_24_sw16[4]),
    .sw13(dipswitch_24_sw16[3]), .sw14(dipswitch_24_sw16[2]), .sw15(dipswitch_24_sw16[1]),
    .sw16(dipswitch_24_sw16[0]));
  DipSwitch #(.number(16)) dipswitch_25 (
    .sw1(dipswitch_25_sw16[15]), .sw2(dipswitch_25_sw16[14]), .sw3(dipswitch_25_sw16[13]),
    .sw4(dipswitch_25_sw16[12]), .sw5(dipswitch_25_sw16[11]), .sw6(dipswitch_25_sw16[10]),
    .sw7(dipswitch_25_sw16[9]), .sw8(dipswitch_25_sw16[8]), .sw9(dipswitch_25_sw16[7]),
    .sw10(dipswitch_25_sw16[6]), .sw11(dipswitch_25_sw16[5]), .sw12(dipswitch_25_sw16[4]),
    .sw13(dipswitch_25_sw16[3]), .sw14(dipswitch_25_sw16[2]), .sw15(dipswitch_25_sw16[1]),
    .sw16(dipswitch_25_sw16[0]));
  DipSwitch #(.number(16)) dipswitch_26 (
    .sw1(dipswitch_26_sw8[15]), .sw2(dipswitch_26_sw8[14]), .sw3(dipswitch_26_sw8[13]),
    .sw4(dipswitch_26_sw8[12]), .sw5(dipswitch_26_sw8[11]), .sw6(dipswitch_26_sw8[10]),
    .sw7(dipswitch_26_sw8[9]), .sw8(dipswitch_26_sw8[8]), .sw9(dipswitch_26_sw16[7]),
    .sw10(dipswitch_26_sw16[6]), .sw11(dipswitch_26_sw16[5]), .sw12(dipswitch_26_sw16[4]),
    .sw13(dipswitch_26_sw16[3]), .sw14(dipswitch_26_sw16[2]), .sw15(dipswitch_26_sw16[1]),
    .sw16(dipswitch_26_sw16[0]));
  not not_1 (not_1_out, button_1_out);
  Button button_1 (.out(button_1_out));
  not not_2 (not_2_out, button_2_out);
  Button button_2 (.out(button_2_out));
  DipSwitch #(.number(3)) dipswitch_27 (.sw1(dipswitch_27_sw1), .sw2(dipswitch_27_sw2), .sw3(dipswitch_27_sw3));
  DipSwitch #(.number(3)) dipswitch_28 (
    .sw1(dipswitch_28_sw3[2]), .sw2(dipswitch_28_sw3[1]), .sw3(dipswitch_28_sw3[0]));
  DipSwitch #(.number(4)) dipswitch_29 (
    .sw1(dipswitch_29_sw4[3]), .sw2(dipswitch_29_sw4[2]), .sw3(dipswitch_29_sw4[1]), .sw4(dipswitch_29_sw4[0]));
  DipSwitch #(.number(4)) dipswitch_30 (
    .sw1(dipswitch_30_sw1), .sw2(dipswitch_30_sw2), .sw3(dipswitch_30_sw3), .sw4(dipswitch_30_sw4));
  not not_3 (not_3_out, dipswitch_27_sw2);
  DipSwitch #(.number(3)) dipswitch_31 (
    .sw1(dipswitch_31_sw3[2]), .sw2(dipswitch_31_sw3[1]), .sw3(dipswitch_31_sw3[0]));
  DipSwitch #(.number(3)) dipswitch_32 (
    .sw1(dipswitch_32_sw3[2]), .sw2(dipswitch_32_sw3[1]), .sw3(dipswitch_32_sw3[0]));
  DipSwitch #(.number(3)) dipswitch_33 (
    .sw1(dipswitch_33_sw3[2]), .sw2(dipswitch_33_sw3[1]), .sw3(dipswitch_33_sw3[0]));
  DipSwitch #(.number(2)) dipswitch_34 (.sw2(dipswitch_34_sw2));  // open: sw1
  DipSwitch #(.number(2)) dipswitch_35 (.sw2(dipswitch_35_sw2));  // open: sw1
  DipSwitch #(.number(3)) dipswitch_36 (.sw1(dipswitch_36_sw1), .sw2(dipswitch_36_sw2), .sw3(dipswitch_36_sw3));
  DipSwitch #(.number(2)) dipswitch_37 (.sw1(dipswitch_37_sw1), .sw2(dipswitch_37_sw2));
  DipSwitch #(.number(2)) dipswitch_38 (.sw1(dipswitch_38_sw1), .sw2(dipswitch_38_sw2));
  DipSwitch #(.number(2)) dipswitch_39 (.sw2(dipswitch_39_sw2));  // open: sw1
  DipSwitch #(.number(3)) dipswitch_40 (
    .sw1(dipswitch_40_sw3[2]), .sw2(dipswitch_40_sw3[1]), .sw3(dipswitch_40_sw3[0]));
  DipSwitch #(.number(4)) dipswitch_41 (
    .sw1(dipswitch_41_sw4[3]), .sw2(dipswitch_41_sw4[2]), .sw3(dipswitch_41_sw4[1]), .sw4(dipswitch_41_sw4[0]));
  RAM #(.addrWidth(15), .asyncread("true"), .byteenables("byteEnables"), .dataWidth(16)) ram_1 (
    .addr({15{1'b0}}), .we(dipswitch_30_sw1), .oe(dipswitch_30_sw2), .clk(undriven),
    .din({dipswitch_26_sw8, dipswitch_26_sw16}), .dout(ram_1_dout), .be1(dipswitch_30_sw3),
    .be0(dipswitch_30_sw4));
  DipSwitch #(.number(3)) dipswitch_42 (.sw1(dipswitch_42_sw1), .sw2(dipswitch_42_sw2), .sw3(dipswitch_42_sw3));
  DipSwitch #(.number(16)) dipswitch_43 (
    .sw1(dipswitch_43_sw16[15]), .sw2(dipswitch_43_sw16[14]), .sw3(dipswitch_43_sw16[13]),
    .sw4(dipswitch_43_sw16[12]), .sw5(dipswitch_43_sw16[11]), .sw6(dipswitch_43_sw16[10]),
    .sw7(dipswitch_43_sw16[9]), .sw8(dipswitch_43_sw16[8]), .sw9(dipswitch_43_sw16[7]),
    .sw10(dipswitch_43_sw16[6]), .sw11(dipswitch_43_sw16[5]), .sw12(dipswitch_43_sw16[4]),
    .sw13(dipswitch_43_sw16[3]), .sw14(dipswitch_43_sw16[2]), .sw15(dipswitch_43_sw16[1]),
    .sw16(dipswitch_43_sw16[0]));
  not not_4 (not_4_out, dipswitch_44_sw2);
  Reg16Buf reg16buf_1 (
    .CLK(undriven), .nWE(dipswitch_18_sw1), .D(dipswitch_1_sw16), .nOE(dipswitch_18_sw2), .Q(reg16buf_1_q));  // open: DBG_Q
  RegPC regpc_1 (
    .nCLR(not_1_out), .CLK(undriven), .CNTE(1'b1), .nWE(not_2_out), .D(dipswitch_1_sw16),
    .nOE(dipswitch_19_sw2), .PC0(dipswitch_19_sw1), .QPC(regpc_1_qpc), .Q(regpc_1_q));
  Ram8_16 ram8_16_1 (
    .A(dipswitch_2_sw16), .CLK(undriven), .DI(buf16_1_do), .OE(dipswitch_27_sw3), .WE(dipswitch_27_sw2),
    .W16(dipswitch_27_sw1), .DO(ram8_16_1_do));
  Buf16 buf16_1 (.DI(dipswitch_3_sw16), .nOE(not_3_out), .DO(buf16_1_do));
  RegFileOld regfileold_1 (
    .CLK(undriven), .D(dipswitch_4_sw16), .DSEL(dipswitch_28_sw3), .WE(dipswitch_20_sw1),
    .QSEL0(dipswitch_31_sw3), .OE0(dipswitch_20_sw3), .QSEL1(dipswitch_32_sw3), .OE1(dipswitch_20_sw4),
    .nPCCLR(not_5_out), .PCCNTE(1'b1), .PC0(1'b0), .Q0(regfileold_1_q0), .Q1(regfileold_1_q1),
    .QPC(regfileold_1_qpc));  // open: DBG_R0, DBG_R1, DBG_R2, DBG_R3, DBG_R4, DBG_R5, DBG_R6
  InstrCompressor instrcompressor_1 (.INSTRI(dipswitch_6_sw16), .INSTRO(instrcompressor_1_instro));
  BitRev16 bitrev16_1 (.DI(dipswitch_7_sw16), .REV(dipswitch_35_sw2), .DO(bitrev16_1_do));
  Ram8_16 ram8_16_2 (
    .A(dipswitch_8_sw16), .CLK(undriven), .DI(buf16_2_do), .OE(dipswitch_37_sw2), .WE(dipswitch_37_sw1),
    .W16(1'b1), .DO(ram8_16_2_do));
  DipSwitch #(.number(2)) dipswitch_44 (.sw2(dipswitch_44_sw2));  // open: sw1
  Buf16 buf16_2 (.DI(dipswitch_43_sw16), .nOE(not_4_out), .DO(buf16_2_do));
  Adder16 adder16_1 (
    .DI0(dipswitch_9_sw16), .DI1(dipswitch_10_sw16), .CI(dipswitch_38_sw1), .SUB(dipswitch_38_sw2),
    .DO(adder16_1_do), .CO(adder16_1_co), .OVF(adder16_1_ovf));
  LED led_1 (.in(adder16_1_co));
  LED led_2 (.in(adder16_1_ovf));
  ALU alu_1 (
    .DIL(dipswitch_11_sw16), .DIR(dipswitch_12_sw16), .OP(dipswitch_29_sw4), .CI(dipswitch_39_sw2),
    .DO(alu_1_do), .CO(alu_1_co), .Z(alu_1_z), .S(alu_1_s), .OVF(alu_1_ovf));
  LED led_3 (.in(alu_1_co));
  LED led_4 (.in(alu_1_z));
  LED led_5 (.in(alu_1_s));
  LED led_6 (.in(alu_1_ovf));
  CondDecoder conddecoder_1 (.INSTR(dipswitch_13_sw16), .CONDCODE(conddecoder_1_condcode));
  LED led_7 (.in(sel1of8_1_do));
  Sel1of8 sel1of8_1 (.DI(dipswitch_14_sw8), .SEL(dipswitch_40_sw3), .DO(sel1of8_1_do));
  LED led_8 (.in(condeval_1_condval));
  CondEval condeval_1 (
    .C(dipswitch_23_sw4), .Z(dipswitch_23_sw3), .S(dipswitch_23_sw2), .O(dipswitch_23_sw1),
    .CONDCODE(dipswitch_41_sw4), .CONDVAL(condeval_1_condval));
  ALU alu_2 (
    .DIL(dipswitch_24_sw16), .DIR(dipswitch_25_sw16), .OP(4'b1001), .CI(1'b0), .CO(alu_2_co), .Z(alu_2_z),
    .S(alu_2_s), .OVF(alu_2_ovf));  // open: DO
  RegCnt8 regcnt8_1 (.nCLR(1'b1), .CLK(undriven), .CNTE(1'b1), .D({8{1'b0}}), .nWE(1'b1), .Q(regcnt8_1_q));  // open: TC
  MemIf8_16w memif8_16w_1 (
    .MDI(dipswitch_15_sw16), .AI(dipswitch_17_sw22), .DI(dipswitch_16_sw16), .OE(dipswitch_42_sw1),
    .WE(dipswitch_42_sw2), .W16(dipswitch_42_sw3), .AO(memif8_16w_1_ao), .MDO(memif8_16w_1_mdo),
    .DO(memif8_16w_1_do), .BothOE(memif8_16w_1_bothoe), .BothWE(memif8_16w_1_bothwe),
    .EvenE(memif8_16w_1_evene), .OddE(memif8_16w_1_odde));
  LED led_9 (.in(memif8_16w_1_bothoe));
  LED led_10 (.in(memif8_16w_1_bothwe));
  LED led_11 (.in(memif8_16w_1_evene));
  LED led_12 (.in(memif8_16w_1_odde));
  Hex_Digit_Display hex_digit_display_1 (.value(reg16buf_1_q[15:12]));  // open: dp
  Hex_Digit_Display hex_digit_display_2 (.value(reg16buf_1_q[11:8]));  // open: dp
  Hex_Digit_Display hex_digit_display_3 (.value(regpc_1_qpc[15:12]));  // open: dp
  Hex_Digit_Display hex_digit_display_4 (.value(regpc_1_qpc[11:8]));  // open: dp
  Hex_Digit_Display hex_digit_display_5 (.value(regpc_1_q[15:12]));  // open: dp
  Hex_Digit_Display hex_digit_display_6 (.value(regpc_1_q[11:8]));  // open: dp
  ImmDecoder immdecoder_1 (
    .INSTR(dipswitch_5_sw16), .SEL(dipswitch_33_sw3), .nOE(1'b0), .CONDVAL(dipswitch_34_sw2),
    .IMM(immdecoder_1_imm));
  Hex_Digit_Display hex_digit_display_7 (.value(bitrev16_1_do[15:12]));  // open: dp
  Shifter16 shifter16_1 (
    .DI(dipswitch_21_sw16), .LEFT(dipswitch_36_sw1), .SEXT(dipswitch_36_sw2), .ROT(dipswitch_36_sw3),
    .CNT(dipswitch_22_sw16), .DO(shifter16_1_do));
  Hex_Digit_Display hex_digit_display_8 (.value(adder16_1_do[15:12]));  // open: dp
  Hex_Digit_Display hex_digit_display_9 (.value(alu_1_do[15:12]));  // open: dp
  Hex_Digit_Display hex_digit_display_10 (.value(conddecoder_1_condcode));  // open: dp
  assign bit_extender_1_out = {{3{1'b0}}, memif8_16w_1_ao};  // Bit_Extender bit_extender_1
  Hex_Digit_Display hex_digit_display_11 (.value(reg16buf_1_q[7:4]));  // open: dp
  Hex_Digit_Display hex_digit_display_12 (.value(regpc_1_qpc[7:4]));  // open: dp
  Hex_Digit_Display hex_digit_display_13 (.value(regpc_1_q[7:4]));  // open: dp
  Hex_Digit_Display hex_digit_display_14 (.value(ram8_16_1_do[15:12]));  // open: dp
  Hex_Digit_Display hex_digit_display_15 (.value(ram8_16_1_do[11:8]));  // open: dp
  Hex_Digit_Display hex_digit_display_16 (.value(regfileold_1_q0[15:12]));  // open: dp
  Hex_Digit_Display hex_digit_display_17 (.value(regfileold_1_q0[11:8]));  // open: dp
  Hex_Digit_Display hex_digit_display_18 (.value(regfileold_1_q1[15:12]));  // open: dp
  Hex_Digit_Display hex_digit_display_19 (.value(regfileold_1_q1[11:8]));  // open: dp
  Hex_Digit_Display hex_digit_display_20 (.value(regfileold_1_qpc[15:12]));  // open: dp
  Hex_Digit_Display hex_digit_display_21 (.value(regfileold_1_qpc[11:8]));  // open: dp
  Hex_Digit_Display hex_digit_display_22 (.value(immdecoder_1_imm[15:12]));  // open: dp
  Hex_Digit_Display hex_digit_display_23 (.value(bitrev16_1_do[11:8]));  // open: dp
  Hex_Digit_Display hex_digit_display_24 (.value(shifter16_1_do[15:12]));  // open: dp
  Hex_Digit_Display hex_digit_display_25 (.value(shifter16_1_do[11:8]));  // open: dp
  Hex_Digit_Display hex_digit_display_26 (.value(ram8_16_2_do[15:12]));  // open: dp
  Hex_Digit_Display hex_digit_display_27 (.value(ram8_16_2_do[11:8]));  // open: dp
  DipSwitch #(.number(3)) dipswitch_45 (
    .sw1(dipswitch_45_sw3[2]), .sw2(dipswitch_45_sw3[1]), .sw3(dipswitch_45_sw3[0]));
  DipSwitch #(.number(3)) dipswitch_46 (
    .sw1(dipswitch_46_sw3[2]), .sw2(dipswitch_46_sw3[1]), .sw3(dipswitch_46_sw3[0]));
  Hex_Digit_Display hex_digit_display_28 (.value(adder16_1_do[11:8]));  // open: dp
  Hex_Digit_Display hex_digit_display_29 (.value(adder16_1_do[7:4]));  // open: dp
  Hex_Digit_Display hex_digit_display_30 (.value(alu_1_do[11:8]));  // open: dp
  Hex_Digit_Display hex_digit_display_31 (.value(alu_1_do[7:4]));  // open: dp
  Hex_Digit_Display hex_digit_display_32 (.value(bit_extender_1_out[23:20]));  // open: dp
  Hex_Digit_Display hex_digit_display_33 (.value(memif8_16w_1_mdo[15:12]));  // open: dp
  Hex_Digit_Display hex_digit_display_34 (.value(memif8_16w_1_do[15:12]));  // open: dp
  Hex_Digit_Display hex_digit_display_35 (.value(reg16buf_1_q[3:0]));  // open: dp
  Hex_Digit_Display hex_digit_display_36 (.value(regpc_1_qpc[3:0]));  // open: dp
  Hex_Digit_Display hex_digit_display_37 (.value(regpc_1_q[3:0]));  // open: dp
  Hex_Digit_Display hex_digit_display_38 (.value(ram8_16_1_do[7:4]));  // open: dp
  Hex_Digit_Display hex_digit_display_39 (.value(ram8_16_1_do[3:0]));  // open: dp
  DipSwitch #(.number(4)) dipswitch_47 (
    .sw1(dipswitch_47_sw1), .sw2(dipswitch_47_sw2), .sw3(dipswitch_47_sw3), .sw4(dipswitch_47_sw4));
  Hex_Digit_Display hex_digit_display_40 (.value(regfileold_1_q0[7:4]));  // open: dp
  Hex_Digit_Display hex_digit_display_41 (.value(regfileold_1_q1[7:4]));  // open: dp
  Hex_Digit_Display hex_digit_display_42 (.value(regfileold_1_qpc[7:4]));  // open: dp
  not not_5 (not_5_out, button_3_out);
  Hex_Digit_Display hex_digit_display_43 (.value(immdecoder_1_imm[11:8]));  // open: dp
  Hex_Digit_Display hex_digit_display_44 (.value(immdecoder_1_imm[7:4]));  // open: dp
  Hex_Digit_Display hex_digit_display_45 (.value(instrcompressor_1_instro[7:4]));  // open: dp
  Hex_Digit_Display hex_digit_display_46 (.value(instrcompressor_1_instro[3:0]));  // open: dp
  Hex_Digit_Display hex_digit_display_47 (.value(bitrev16_1_do[7:4]));  // open: dp
  Hex_Digit_Display hex_digit_display_48 (.value(bitrev16_1_do[3:0]));  // open: dp
  Hex_Digit_Display hex_digit_display_49 (.value(shifter16_1_do[7:4]));  // open: dp
  Hex_Digit_Display hex_digit_display_50 (.value(ram8_16_2_do[7:4]));  // open: dp
  Hex_Digit_Display hex_digit_display_51 (.value(ram8_16_2_do[3:0]));  // open: dp
  DipSwitch #(.number(2)) dipswitch_48 (.sw1(dipswitch_48_sw1), .sw2(dipswitch_48_sw2));
  Hex_Digit_Display hex_digit_display_52 (.value(adder16_1_do[3:0]));  // open: dp
  Hex_Digit_Display hex_digit_display_53 (.value(alu_1_do[3:0]));  // open: dp
  Hex_Digit_Display hex_digit_display_54 (.value(bit_extender_1_out[19:16]));  // open: dp
  Hex_Digit_Display hex_digit_display_55 (.value(bit_extender_1_out[15:12]));  // open: dp
  Hex_Digit_Display hex_digit_display_56 (.value(memif8_16w_1_mdo[11:8]));  // open: dp
  Hex_Digit_Display hex_digit_display_57 (.value(memif8_16w_1_mdo[7:4]));  // open: dp
  Hex_Digit_Display hex_digit_display_58 (.value(memif8_16w_1_do[11:8]));  // open: dp
  Hex_Digit_Display hex_digit_display_59 (.value(memif8_16w_1_do[7:4]));  // open: dp
  Hex_Digit_Display hex_digit_display_60 (.value(regfileold_1_q0[3:0]));  // open: dp
  Hex_Digit_Display hex_digit_display_61 (.value(regfileold_1_q1[3:0]));  // open: dp
  Hex_Digit_Display hex_digit_display_62 (.value(regfileold_1_qpc[3:0]));  // open: dp
  Button button_3 (.out(button_3_out));
  Hex_Digit_Display hex_digit_display_63 (.value(immdecoder_1_imm[3:0]));  // open: dp
  Hex_Digit_Display hex_digit_display_64 (.value(shifter16_1_do[3:0]));  // open: dp
  not not_6 (not_6_out, n74138_1_pin15);
  _74138 u_74138_1 (
    .pin1(regcnt8_1_q[0]), .pin2(regcnt8_1_q[1]), .pin3(regcnt8_1_q[2]), .pin4(n74138_1_pin4),
    .pin5(n74138_1_pin4), .pin6(n74138_1_pin6), .pin15(n74138_1_pin15), .pin14(n74138_1_pin14),
    .pin12(n74138_1_pin12), .pin11(n74138_1_pin11), .pin10(n74138_1_pin10));  // open: pin7, pin13, pin9
  Hex_Digit_Display hex_digit_display_65 (.value(bit_extender_1_out[11:8]));  // open: dp
  Hex_Digit_Display hex_digit_display_66 (.value(bit_extender_1_out[7:4]));  // open: dp
  Hex_Digit_Display hex_digit_display_67 (.value(memif8_16w_1_mdo[3:0]));  // open: dp
  Hex_Digit_Display hex_digit_display_68 (.value(memif8_16w_1_do[3:0]));  // open: dp
  CondEval condeval_2 (
    .C(alu_2_co), .Z(alu_2_z), .S(alu_2_s), .O(alu_2_ovf), .CONDCODE({1'b0, regcnt8_1_q[2:0]}),
    .CONDVAL(condeval_2_condval));
  not not_7 (not_7_out, n74138_1_pin14);
  not not_8 (not_8_out, n74138_1_pin12);
  not not_9 (not_9_out, n74138_1_pin11);
  Hex_Digit_Display hex_digit_display_69 (.value(bit_extender_1_out[3:0]));  // open: dp
  RamProt ramprot_1 (
    .OEI(dipswitch_47_sw1), .WEI(dipswitch_47_sw2), .A0(dipswitch_47_sw3), .W16(dipswitch_47_sw4),
    .OEO(ramprot_1_oeo), .WEO(ramprot_1_weo));
  RegFileOld regfileold_2 (
    .CLK(undriven), .D(ram8_16_2_do), .DSEL(dipswitch_45_sw3), .WE(dipswitch_48_sw1),
    .QSEL0(dipswitch_46_sw3), .OE0(dipswitch_48_sw2), .QSEL1(dipswitch_46_sw3), .OE1(dipswitch_48_sw2),
    .nPCCLR(1'b1), .PCCNTE(1'b1), .PC0(1'b0), .Q0(buf16_2_do), .QPC(regfileold_2_qpc));  // open: Q1, DBG_R0, DBG_R1, DBG_R2, DBG_R3, DBG_R4, DBG_R5, DBG_R6
  not not_10 (not_10_out, n74138_1_pin10);
  LED led_13 (.in(ramprot_1_oeo));
  LED led_14 (.in(ramprot_1_weo));
  Hex_Digit_Display hex_digit_display_70 (.value(regfileold_2_qpc[15:12]));  // open: dp
  Register #(.width(1)) register_1 (
    .D(condeval_2_condval), .en(not_7_out), .clk(undriven), .Q(register_1_q), .clr(1'b0));
  Register #(.width(1)) register_2 (
    .D(condeval_2_condval), .en(not_6_out), .clk(undriven), .Q(register_2_q), .clr(1'b0));
  Register #(.width(1)) register_3 (
    .D(condeval_2_condval), .en(not_8_out), .clk(undriven), .Q(register_3_q), .clr(1'b0));
  Register #(.width(1)) register_4 (
    .D(condeval_2_condval), .en(not_9_out), .clk(undriven), .Q(register_4_q), .clr(1'b0));
  Register #(.width(1)) register_5 (
    .D(condeval_2_condval), .en(not_10_out), .clk(undriven), .Q(register_5_q), .clr(1'b0));
  Hex_Digit_Display hex_digit_display_71 (.value(regfileold_2_qpc[11:8]));  // open: dp
  Hex_Digit_Display hex_digit_display_72 (.value(regfileold_2_qpc[7:4]));  // open: dp
  LED led_15 (.in(register_1_q));
  LED led_16 (.in(register_2_q));
  LED led_17 (.in(register_3_q));
  LED led_18 (.in(register_4_q));
  LED led_19 (.in(register_5_q));
  Hex_Digit_Display hex_digit_display_73 (.value(regfileold_2_qpc[3:0]));  // open: dp
  // also tied to GND on the sheet: n74138_1_pin4
  // also tied to VCC on the sheet: n74138_1_pin6

  // Notes on the sheet:
  //   0: sr
  //   1: sl
  //   2: rr
  //   3: rl
  //   4: asr
  //   5: reserved
  //   6: reserved
  //   7: xor
  //   8: add
  //   9: sub/cmp
  //   10: adc
  //   11: sbb
  //   12: zxt
  //   13: sxt
  //   14: and
  //   15: or
  //   0: C/LU
  //   1: Z/E
  //   2: S
  //   3: LEU
  //   4: L
  //   5: LE
  //   6: O
  //   7: NO
  //   8: NC/GEU
  //   9: NZ/NE
  //   10: NS
  //   11: GU
  //   12: GE
  //   13: G
  //   9: sub/cmp
  //   Equal
  //   < unsigned
  //   <= unsigned
  //   < signed
  //   <= signed
endmodule

module And8 (
  input  [7:0] DI0,
  input  [7:0] DI1,
  output [7:0] DO
);

  _7408 u_7408_1 (
    .pin1(DI1[5]), .pin2(DI0[5]), .pin3(DO[5]), .pin4(DI1[4]), .pin5(DI0[4]), .pin6(DO[4]), .pin13(DI1[6]),
    .pin12(DI0[6]), .pin11(DO[6]), .pin10(DI1[7]), .pin9(DI0[7]), .pin8(DO[7]));
  _7408 u_7408_2 (
    .pin1(DI1[1]), .pin2(DI0[1]), .pin3(DO[1]), .pin4(DI1[0]), .pin5(DI0[0]), .pin6(DO[0]), .pin13(DI1[2]),
    .pin12(DI0[2]), .pin11(DO[2]), .pin10(DI1[3]), .pin9(DI0[3]), .pin8(DO[3]));
endmodule

module And16 (
  input  [15:0] DI0,
  input  [15:0] DI1,
  output [15:0] DO
);

  And8 and8_1 (.DI0(DI0[7:0]), .DI1(DI1[7:0]), .DO(DO[7:0]));
  And8 and8_2 (.DI0(DI0[15:8]), .DI1(DI1[15:8]), .DO(DO[15:8]));
endmodule

module Or8 (
  input  [7:0] DI0,
  input  [7:0] DI1,
  output [7:0] DO
);

  _7432 u_7432_1 (
    .pin1(DI1[5]), .pin2(DI0[5]), .pin3(DO[5]), .pin4(DI1[4]), .pin5(DI0[4]), .pin6(DO[4]), .pin13(DI1[6]),
    .pin12(DI0[6]), .pin11(DO[6]), .pin10(DI1[7]), .pin9(DI0[7]), .pin8(DO[7]));
  _7432 u_7432_2 (
    .pin1(DI1[1]), .pin2(DI0[1]), .pin3(DO[1]), .pin4(DI1[0]), .pin5(DI0[0]), .pin6(DO[0]), .pin13(DI1[2]),
    .pin12(DI0[2]), .pin11(DO[2]), .pin10(DI1[3]), .pin9(DI0[3]), .pin8(DO[3]));
endmodule

module Or16 (
  input  [15:0] DI0,
  input  [15:0] DI1,
  output [15:0] DO
);

  Or8 or8_1 (.DI0(DI0[7:0]), .DI1(DI1[7:0]), .DO(DO[7:0]));
  Or8 or8_2 (.DI0(DI0[15:8]), .DI1(DI1[15:8]), .DO(DO[15:8]));
endmodule

module Xor8 (
  input  [7:0] DI0,
  input  [7:0] DI1,
  output [7:0] DO
);

  _7486 u_7486_1 (
    .pin1(DI1[5]), .pin2(DI0[5]), .pin3(DO[5]), .pin4(DI1[4]), .pin5(DI0[4]), .pin6(DO[4]), .pin13(DI1[6]),
    .pin12(DI0[6]), .pin11(DO[6]), .pin10(DI1[7]), .pin9(DI0[7]), .pin8(DO[7]));
  _7486 u_7486_2 (
    .pin1(DI1[1]), .pin2(DI0[1]), .pin3(DO[1]), .pin4(DI1[0]), .pin5(DI0[0]), .pin6(DO[0]), .pin13(DI1[2]),
    .pin12(DI0[2]), .pin11(DO[2]), .pin10(DI1[3]), .pin9(DI0[3]), .pin8(DO[3]));
endmodule

module Xor16 (
  input  [15:0] DI0,
  input  [15:0] DI1,
  output [15:0] DO
);

  Xor8 xor8_1 (.DI0(DI0[7:0]), .DI1(DI1[7:0]), .DO(DO[7:0]));
  Xor8 xor8_2 (.DI0(DI0[15:8]), .DI1(DI1[15:8]), .DO(DO[15:8]));
endmodule

module Add8 (
  input  [7:0] DI0,
  input  [7:0] DI1,
  input  CI,
  output [7:0] DO,
  output CO
);

  wire n74283_1_pin7;

  _74283 u_74283_1 (
    .pin1(DO[5]), .pin2(DI1[5]), .pin3(DI0[5]), .pin4(DO[4]), .pin5(DI0[4]), .pin6(DI1[4]),
    .pin7(n74283_1_pin7), .pin15(DI1[6]), .pin14(DI0[6]), .pin13(DO[6]), .pin12(DI0[7]), .pin11(DI1[7]),
    .pin10(DO[7]), .pin9(CO));
  _74283 u_74283_2 (
    .pin1(DO[1]), .pin2(DI1[1]), .pin3(DI0[1]), .pin4(DO[0]), .pin5(DI0[0]), .pin6(DI1[0]), .pin7(CI),
    .pin15(DI1[2]), .pin14(DI0[2]), .pin13(DO[2]), .pin12(DI0[3]), .pin11(DI1[3]), .pin10(DO[3]),
    .pin9(n74283_1_pin7));
endmodule

module Add16 (
  input  [15:0] DI0,
  input  [15:0] DI1,
  input  CI,
  output [15:0] DO,
  output CO
);

  wire add8_1_co;

  Add8 add8_1 (.DI0(DI0[7:0]), .DI1(DI1[7:0]), .CI(CI), .DO(DO[7:0]), .CO(add8_1_co));
  Add8 add8_2 (.DI0(DI0[15:8]), .DI1(DI1[15:8]), .CI(add8_1_co), .DO(DO[15:8]), .CO(CO));
endmodule

module Buf8 (
  input  [7:0] DI,
  input  nOE,
  output [7:0] DO
);

  _74244 u_74244_1 (
    .pin1(nOE), .pin2(DI[4]), .pin3(DO[3]), .pin4(DI[5]), .pin5(DO[2]), .pin6(DI[6]), .pin7(DO[1]),
    .pin8(DI[7]), .pin9(DO[0]), .pin19(nOE), .pin18(DO[4]), .pin17(DI[3]), .pin16(DO[5]), .pin15(DI[2]),
    .pin14(DO[6]), .pin13(DI[1]), .pin12(DO[7]), .pin11(DI[0]));
endmodule

module Buf16 (
  input  [15:0] DI,
  input  nOE,
  output [15:0] DO
);

  Buf8 buf8_1 (.DI(DI[7:0]), .nOE(nOE), .DO(DO[7:0]));
  Buf8 buf8_2 (.DI(DI[15:8]), .nOE(nOE), .DO(DO[15:8]));
endmodule

module Sel1 (
  input  DI0,
  input  DI1,
  input  SEL,
  output DO
);

  wire n7400_1_pin3, n7400_1_pin5, n7400_1_pin11;

  _7400 u_7400_1 (
    .pin1(DI1), .pin2(SEL), .pin3(n7400_1_pin3), .pin4(n7400_1_pin3), .pin5(n7400_1_pin5), .pin6(DO),
    .pin13(SEL), .pin12(SEL), .pin11(n7400_1_pin11), .pin10(n7400_1_pin11), .pin9(DI0), .pin8(n7400_1_pin5));
endmodule

module Sel4 (
  input  [3:0] DI0,
  input  [3:0] DI1,
  input  SEL,
  output [3:0] DO
);

  wire n74157_1_pin15;

  _74157 u_74157_1 (
    .pin1(SEL), .pin2(DI0[3]), .pin3(DI1[3]), .pin4(DO[3]), .pin5(DI0[2]), .pin6(DI1[2]), .pin7(DO[2]),
    .pin15(n74157_1_pin15), .pin14(DI0[1]), .pin13(DI1[1]), .pin12(DO[1]), .pin11(DI0[0]), .pin10(DI1[0]),
    .pin9(DO[0]));
  // also tied to GND on the sheet: n74157_1_pin15
endmodule

module Sel8 (
  input  [7:0] DI0,
  input  [7:0] DI1,
  input  SEL,
  output [7:0] DO
);

  Sel4 sel4_1 (.DI0(DI0[3:0]), .DI1(DI1[3:0]), .SEL(SEL), .DO(DO[3:0]));
  Sel4 sel4_2 (.DI0(DI0[7:4]), .DI1(DI1[7:4]), .SEL(SEL), .DO(DO[7:4]));
endmodule

module Sel16 (
  input  [15:0] DI0,
  input  [15:0] DI1,
  input  SEL,
  output [15:0] DO
);

  Sel8 sel8_1 (.DI0(DI0[7:0]), .DI1(DI1[7:0]), .SEL(SEL), .DO(DO[7:0]));
  Sel8 sel8_2 (.DI0(DI0[15:8]), .DI1(DI1[15:8]), .SEL(SEL), .DO(DO[15:8]));
endmodule

module Sel1of8 (
  input  [7:0] DI,
  input  [2:0] SEL,
  output DO
);

  wire n7404_1_pin1, n7404_1_pin8, n7404_1_pin10, n7404_1_pin12, n7430_1_pin1, n7430_1_pin2, n7430_1_pin3,
       n7430_1_pin4, n7430_1_pin5, n7430_1_pin6, n7430_1_pin11, n7430_1_pin12;

  _7404 u_7404_1 (
    .pin1(n7404_1_pin1), .pin3(n7404_1_pin1), .pin5(n7404_1_pin1), .pin13(SEL[0]), .pin12(n7404_1_pin12),
    .pin11(SEL[1]), .pin10(n7404_1_pin10), .pin9(SEL[2]), .pin8(n7404_1_pin8));  // open: pin2, pin4, pin6
  _7430 u_7430_1 (
    .pin1(n7430_1_pin1), .pin2(n7430_1_pin2), .pin3(n7430_1_pin3), .pin4(n7430_1_pin4), .pin5(n7430_1_pin5),
    .pin6(n7430_1_pin6), .pin12(n7430_1_pin12), .pin11(n7430_1_pin11), .pin8(DO));  // open: pin13, pin10, pin9
  _7420 u_7420_1 (
    .pin1(SEL[0]), .pin2(n7404_1_pin10), .pin4(n7404_1_pin8), .pin5(DI[1]), .pin6(n7430_1_pin2),
    .pin13(n7404_1_pin8), .pin12(n7404_1_pin10), .pin10(n7404_1_pin12), .pin9(DI[0]), .pin8(n7430_1_pin1));  // open: pin3, pin11
  _7420 u_7420_2 (
    .pin1(SEL[0]), .pin2(SEL[1]), .pin4(n7404_1_pin8), .pin5(DI[3]), .pin6(n7430_1_pin4),
    .pin13(n7404_1_pin8), .pin12(n7404_1_pin12), .pin10(SEL[1]), .pin9(DI[2]), .pin8(n7430_1_pin3));  // open: pin3, pin11
  _7420 u_7420_3 (
    .pin1(SEL[0]), .pin2(SEL[2]), .pin4(n7404_1_pin10), .pin5(DI[5]), .pin6(n7430_1_pin6),
    .pin13(n7404_1_pin10), .pin12(n7404_1_pin12), .pin10(SEL[2]), .pin9(DI[4]), .pin8(n7430_1_pin5));  // open: pin3, pin11
  _7420 u_7420_4 (
    .pin1(SEL[0]), .pin2(SEL[1]), .pin4(SEL[2]), .pin5(DI[7]), .pin6(n7430_1_pin12), .pin13(n7404_1_pin12),
    .pin12(SEL[2]), .pin10(SEL[1]), .pin9(DI[6]), .pin8(n7430_1_pin11));  // open: pin3, pin11
  // also tied to GND on the sheet: n7404_1_pin1

  // Notes on the sheet:
  //   Use e.g. 74151 instead
endmodule

module BitRev16 (
  input  [15:0] DI,
  input  REV,
  output [15:0] DO
);

  Sel16 sel16_1 (
    .DI0(DI),
    .DI1({DI[0], DI[1], DI[2], DI[3], DI[4], DI[5], DI[6], DI[7], DI[8], DI[9], DI[10], DI[11], DI[12], DI[13], DI[14], DI[15]}),
    .SEL(REV), .DO(DO));
endmodule

module Reg8 (
  input  CLK,
  input  nWE,
  input  [7:0] D,
  output [7:0] Q
);

  _74377 u_74377_1 (
    .pin1(nWE), .pin2(Q[4]), .pin3(D[4]), .pin4(D[5]), .pin5(Q[5]), .pin6(Q[6]), .pin7(D[6]), .pin8(D[7]),
    .pin9(Q[7]), .pin19(Q[3]), .pin18(D[3]), .pin17(D[2]), .pin16(Q[2]), .pin15(Q[1]), .pin14(D[1]),
    .pin13(D[0]), .pin12(Q[0]), .pin11(CLK));
endmodule

module Reg8Buf (
  input  CLK,
  input  nWE,
  input  [7:0] D,
  input  nOE,
  output [7:0] Q,
  output [7:0] DBG_Q
);

  Reg8 reg8_1 (.CLK(CLK), .nWE(nWE), .D(D), .Q(DBG_Q));
  Buf8 buf8_1 (.DI(DBG_Q), .nOE(nOE), .DO(Q));

  // Notes on the sheet:
  //   4 x 74173
  //   2 x 74380?
  //   2 x 74825
  //   2 x 742825
  //   Possible alternatives with built-in buffers:
  //   May be harder to debug though.
endmodule

module Reg8Buf2 (
  input  CLK,
  input  nWE,
  input  [7:0] D,
  input  nOE0,
  input  nOE1,
  output [7:0] Q0,
  output [7:0] Q1,
  output [7:0] DBG_Q
);

  Reg8 reg8_1 (.CLK(CLK), .nWE(nWE), .D(D), .Q(DBG_Q));
  Buf8 buf8_1 (.DI(DBG_Q), .nOE(nOE0), .DO(Q0));
  Buf8 buf8_2 (.DI(DBG_Q), .nOE(nOE1), .DO(Q1));
endmodule

module Reg16 (
  input  CLK,
  input  nWE,
  input  [15:0] D,
  output [15:0] Q
);

  Reg8 reg8_1 (.CLK(CLK), .nWE(nWE), .D(D[7:0]), .Q(Q[7:0]));
  Reg8 reg8_2 (.CLK(CLK), .nWE(nWE), .D(D[15:8]), .Q(Q[15:8]));
endmodule

module Reg16Buf (
  input  CLK,
  input  nWE,
  input  [15:0] D,
  input  nOE,
  output [15:0] Q,
  output [15:0] DBG_Q
);

  Reg16 reg16_1 (.CLK(CLK), .nWE(nWE), .D(D), .Q(DBG_Q));
  Buf16 buf16_1 (.DI(DBG_Q), .nOE(nOE), .DO(Q));

  // Notes on the sheet:
  //   4 x 74173
  //   2 x 74380?
  //   2 x 74825
  //   2 x 742825
  //   Possible alternatives with built-in buffers:
  //   May be harder to debug though.
endmodule

module Reg16Buf2 (
  input  CLK,
  input  nWE,
  input  [15:0] D,
  input  nOE0,
  input  nOE1,
  output [15:0] Q0,
  output [15:0] Q1,
  output [15:0] DBG_Q
);

  Reg16 reg16_1 (.CLK(CLK), .nWE(nWE), .D(D), .Q(DBG_Q));
  Buf16 buf16_1 (.DI(DBG_Q), .nOE(nOE0), .DO(Q0));
  Buf16 buf16_2 (.DI(DBG_Q), .nOE(nOE1), .DO(Q1));
endmodule

module RegSP (
  input  CLK,
  input  nWE,
  input  [15:0] D,
  output [15:0] Q
);

  wire [0:0] reg8_1_q;

  Reg8 reg8_1 (.CLK(CLK), .nWE(nWE), .D(D[7:0]), .Q({Q[7:1], reg8_1_q[0]}));
  Reg8 reg8_2 (.CLK(CLK), .nWE(nWE), .D(D[15:8]), .Q(Q[15:8]));
  // NoConnect on reg8_1_q[0]

  assign Q[0] = 1'b0;
endmodule

module RegSPBuf (
  input  CLK,
  input  nWE,
  input  [15:0] D,
  input  nOE,
  output [15:0] Q,
  output [15:0] DBG_Q
);

  RegSP regsp_1 (.CLK(CLK), .nWE(nWE), .D(D), .Q(DBG_Q));
  Buf16 buf16_1 (.DI(DBG_Q), .nOE(nOE), .DO(Q));

  // Notes on the sheet:
  //   4 x 74173
  //   2 x 74380?
  //   2 x 74825
  //   2 x 742825
  //   Possible alternatives with built-in buffers:
  //   May be harder to debug though.
endmodule

module RegSPBuf2 (
  input  CLK,
  input  nWE,
  input  [15:0] D,
  input  nOE0,
  input  nOE1,
  output [15:0] Q0,
  output [15:0] Q1,
  output [15:0] DBG_Q
);

  RegSP regsp_1 (.CLK(CLK), .nWE(nWE), .D(D), .Q(DBG_Q));
  Buf16 buf16_1 (.DI(DBG_Q), .nOE(nOE0), .DO(Q0));
  Buf16 buf16_2 (.DI(DBG_Q), .nOE(nOE1), .DO(Q1));
endmodule

module RegCnt8 (
  input  nCLR,
  input  CLK,
  input  CNTE,
  input  [7:0] D,
  input  nWE,
  output TC,
  output [7:0] Q
);

  wire n74161_1_pin7, n74161_1_pin15;

  _74161 u_74161_1 (
    .pin1(nCLR), .pin2(CLK), .pin3(D[0]), .pin4(D[1]), .pin5(D[2]), .pin6(D[3]), .pin7(n74161_1_pin7),
    .pin15(n74161_1_pin15), .pin14(Q[0]), .pin13(Q[1]), .pin12(Q[2]), .pin11(Q[3]), .pin10(CNTE), .pin9(nWE));
  _74161 u_74161_2 (
    .pin1(nCLR), .pin2(CLK), .pin3(D[4]), .pin4(D[5]), .pin5(D[6]), .pin6(D[7]), .pin7(n74161_1_pin7),
    .pin15(TC), .pin14(Q[4]), .pin13(Q[5]), .pin12(Q[6]), .pin11(Q[7]), .pin10(n74161_1_pin15), .pin9(nWE));
  // also tied to VCC on the sheet: n74161_1_pin7
endmodule

module RegCnt8Buf (
  input  nCLR,
  input  CLK,
  input  nWE,
  input  [7:0] D,
  input  nOE,
  input  CNTE,
  output [7:0] Q,
  output [7:0] DBG_Q,
  output TC
);

  RegCnt8 regcnt8_1 (.nCLR(nCLR), .CLK(CLK), .CNTE(CNTE), .D(D), .nWE(nWE), .TC(TC), .Q(DBG_Q));
  Buf8 buf8_1 (.DI(DBG_Q), .nOE(nOE), .DO(Q));
endmodule

module RegCnt8Buf2 (
  input  nCLR,
  input  CLK,
  input  nWE,
  input  [7:0] D,
  input  nOE0,
  input  nOE1,
  input  CNTE,
  output [7:0] Q0,
  output [7:0] Q1,
  output [7:0] DBG_Q,
  output TC
);

  RegCnt8 regcnt8_1 (.nCLR(nCLR), .CLK(CLK), .CNTE(CNTE), .D(D), .nWE(nWE), .TC(TC), .Q(DBG_Q));
  Buf8 buf8_1 (.DI(DBG_Q), .nOE(nOE0), .DO(Q0));
  Buf8 buf8_2 (.DI(DBG_Q), .nOE(nOE1), .DO(Q1));
endmodule

module RegPC (
  input  nCLR,
  input  CLK,
  input  CNTE,
  input  nWE,
  input  [15:0] D,
  input  nOE,
  input  PC0,
  output [15:0] QPC,
  output [15:0] Q
);

  wire regcnt8_1_tc, regcnt8_2_tc;
  wire [7:7] regcnt8_2_q;

  // NoConnect on D[0]
  RegCnt8 regcnt8_1 (.nCLR(nCLR), .CLK(CLK), .CNTE(CNTE), .D(D[8:1]), .nWE(nWE), .TC(regcnt8_1_tc), .Q(QPC[8:1]));
  // NoConnect on regcnt8_2_tc
  RegCnt8 regcnt8_2 (
    .nCLR(nCLR), .CLK(CLK), .CNTE(regcnt8_1_tc), .D({1'b0, D[15:9]}), .nWE(nWE), .TC(regcnt8_2_tc),
    .Q({regcnt8_2_q[7], QPC[15:9]}));
  // NoConnect on regcnt8_2_q[7]
  Buf16 buf16_1 (.DI({QPC[15:1], PC0}), .nOE(nOE), .DO(Q));

  assign QPC[0] = PC0;
endmodule

module RegPCBuf2 (
  input  nCLR,
  input  CLK,
  input  CNTE,
  input  nWE,
  input  [15:0] D,
  input  nOE0,
  input  nOE1,
  input  PC0,
  output [15:0] QPC,
  output [15:0] Q0,
  output [15:0] Q1
);

  wire regcnt8_1_tc, regcnt8_2_tc;
  wire [7:7] regcnt8_2_q;

  // NoConnect on D[0]
  RegCnt8 regcnt8_1 (.nCLR(nCLR), .CLK(CLK), .CNTE(CNTE), .D(D[8:1]), .nWE(nWE), .TC(regcnt8_1_tc), .Q(QPC[8:1]));
  // NoConnect on regcnt8_2_tc
  RegCnt8 regcnt8_2 (
    .nCLR(nCLR), .CLK(CLK), .CNTE(regcnt8_1_tc), .D({1'b0, D[15:9]}), .nWE(nWE), .TC(regcnt8_2_tc),
    .Q({regcnt8_2_q[7], QPC[15:9]}));
  // NoConnect on regcnt8_2_q[7]
  Buf16 buf16_1 (.DI({QPC[15:1], PC0}), .nOE(nOE0), .DO(Q0));
  Buf16 buf16_2 (.DI({QPC[15:1], PC0}), .nOE(nOE1), .DO(Q1));

  assign QPC[0] = PC0;
endmodule

module RegFile1Port (
  input  CLK,
  input  [15:0] D,
  input  [2:0] DSEL,
  input  WE,
  input  [2:0] QSEL,
  input  OE,
  input  nPCCLR,
  input  PCCNTE,
  input  PC0,
  output [15:0] Q,
  output [15:0] QPC,
  output [15:0] DBG_R0,
  output [15:0] DBG_R1,
  output [15:0] DBG_R2,
  output [15:0] DBG_R3,
  output [15:0] DBG_R4,
  output [15:0] DBG_R5,
  output [15:0] DBG_R6
);

  wire n74138_1_pin4, n74138_1_pin7, n74138_1_pin9, n74138_1_pin10, n74138_1_pin11, n74138_1_pin12,
       n74138_1_pin13, n74138_1_pin14, n74138_1_pin15, n74138_2_pin4, n74138_2_pin7, n74138_2_pin9,
       n74138_2_pin10, n74138_2_pin11, n74138_2_pin12, n74138_2_pin13, n74138_2_pin14, n74138_2_pin15;

  _74138 u_74138_1 (
    .pin1(DSEL[0]), .pin2(DSEL[1]), .pin3(DSEL[2]), .pin4(n74138_1_pin4), .pin5(n74138_1_pin4), .pin6(WE),
    .pin7(n74138_1_pin7), .pin15(n74138_1_pin15), .pin14(n74138_1_pin14), .pin13(n74138_1_pin13),
    .pin12(n74138_1_pin12), .pin11(n74138_1_pin11), .pin10(n74138_1_pin10), .pin9(n74138_1_pin9));
  _74138 u_74138_2 (
    .pin1(QSEL[0]), .pin2(QSEL[1]), .pin3(QSEL[2]), .pin4(n74138_2_pin4), .pin5(n74138_2_pin4), .pin6(OE),
    .pin7(n74138_2_pin7), .pin15(n74138_2_pin15), .pin14(n74138_2_pin14), .pin13(n74138_2_pin13),
    .pin12(n74138_2_pin12), .pin11(n74138_2_pin11), .pin10(n74138_2_pin10), .pin9(n74138_2_pin9));
  Reg16Buf reg16buf_1 (.CLK(CLK), .nWE(n74138_1_pin15), .D(D), .nOE(n74138_2_pin15), .Q(Q), .DBG_Q(DBG_R0));
  Reg16Buf reg16buf_2 (.CLK(CLK), .nWE(n74138_1_pin14), .D(D), .nOE(n74138_2_pin14), .Q(Q), .DBG_Q(DBG_R1));
  Reg16Buf reg16buf_3 (.CLK(CLK), .nWE(n74138_1_pin13), .D(D), .nOE(n74138_2_pin13), .Q(Q), .DBG_Q(DBG_R2));
  Reg16Buf reg16buf_4 (.CLK(CLK), .nWE(n74138_1_pin12), .D(D), .nOE(n74138_2_pin12), .Q(Q), .DBG_Q(DBG_R3));
  Reg16Buf reg16buf_5 (.CLK(CLK), .nWE(n74138_1_pin11), .D(D), .nOE(n74138_2_pin11), .Q(Q), .DBG_Q(DBG_R4));
  Reg16Buf reg16buf_6 (.CLK(CLK), .nWE(n74138_1_pin10), .D(D), .nOE(n74138_2_pin10), .Q(Q), .DBG_Q(DBG_R5));
  RegSPBuf regspbuf_1 (.CLK(CLK), .nWE(n74138_1_pin9), .D(D), .nOE(n74138_2_pin9), .Q(Q), .DBG_Q(DBG_R6));
  RegPC regpc_1 (
    .nCLR(nPCCLR), .CLK(CLK), .CNTE(PCCNTE), .nWE(n74138_1_pin7), .D(D), .nOE(n74138_2_pin7), .PC0(PC0),
    .QPC(QPC), .Q(Q));
  // also tied to GND on the sheet: {n74138_1_pin4, n74138_2_pin4}
endmodule

module RegFileOld (
  input  CLK,
  input  [15:0] D,
  input  [2:0] DSEL,
  input  WE,
  input  [2:0] QSEL0,
  input  OE0,
  input  [2:0] QSEL1,
  input  OE1,
  input  nPCCLR,
  input  PCCNTE,
  input  PC0,
  output [15:0] Q0,
  output [15:0] Q1,
  output [15:0] QPC,
  output [15:0] DBG_R0,
  output [15:0] DBG_R1,
  output [15:0] DBG_R2,
  output [15:0] DBG_R3,
  output [15:0] DBG_R4,
  output [15:0] DBG_R5,
  output [15:0] DBG_R6
);

  RegFile1Port regfile1port_1 (
    .CLK(CLK), .D(D), .DSEL(DSEL), .WE(WE), .QSEL(QSEL0), .OE(OE0), .nPCCLR(nPCCLR), .PCCNTE(PCCNTE),
    .PC0(PC0), .Q(Q0));  // open: QPC, DBG_R0, DBG_R1, DBG_R2, DBG_R3, DBG_R4, DBG_R5, DBG_R6
  RegFile1Port regfile1port_2 (
    .CLK(CLK), .D(D), .DSEL(DSEL), .WE(WE), .QSEL(QSEL1), .OE(OE1), .nPCCLR(nPCCLR), .PCCNTE(PCCNTE),
    .PC0(PC0), .Q(Q1), .QPC(QPC), .DBG_R0(DBG_R0), .DBG_R1(DBG_R1), .DBG_R2(DBG_R2), .DBG_R3(DBG_R3),
    .DBG_R4(DBG_R4), .DBG_R5(DBG_R5), .DBG_R6(DBG_R6));
endmodule

module RegFile (
  input  CLK,
  input  [15:0] D,
  input  [2:0] DSEL,
  input  WE,
  input  [2:0] QSELL,
  input  OEL,
  input  [2:0] QSELR,
  input  OER,
  input  nPCCLR,
  input  PCCNTE,
  input  PC0,
  output [15:0] QL,
  output [15:0] QR,
  output [15:0] QPC,
  output [15:0] DBG_R0,
  output [15:0] DBG_R1,
  output [15:0] DBG_R2,
  output [15:0] DBG_R3,
  output [15:0] DBG_R4,
  output [15:0] DBG_R5,
  output [15:0] DBG_R6
);

  wire n74138_1_pin4, n74138_1_pin7, n74138_1_pin9, n74138_1_pin10, n74138_1_pin11, n74138_1_pin12,
       n74138_1_pin13, n74138_1_pin14, n74138_1_pin15, n74138_2_pin4, n74138_2_pin7, n74138_2_pin9,
       n74138_2_pin10, n74138_2_pin11, n74138_2_pin12, n74138_2_pin13, n74138_2_pin14, n74138_2_pin15,
       n74138_3_pin4, n74138_3_pin7, n74138_3_pin9, n74138_3_pin10, n74138_3_pin11, n74138_3_pin12,
       n74138_3_pin13, n74138_3_pin14, n74138_3_pin15;

  _74138 u_74138_1 (
    .pin1(DSEL[0]), .pin2(DSEL[1]), .pin3(DSEL[2]), .pin4(n74138_1_pin4), .pin5(n74138_1_pin4), .pin6(WE),
    .pin7(n74138_1_pin7), .pin15(n74138_1_pin15), .pin14(n74138_1_pin14), .pin13(n74138_1_pin13),
    .pin12(n74138_1_pin12), .pin11(n74138_1_pin11), .pin10(n74138_1_pin10), .pin9(n74138_1_pin9));
  _74138 u_74138_2 (
    .pin1(QSELL[0]), .pin2(QSELL[1]), .pin3(QSELL[2]), .pin4(n74138_2_pin4), .pin5(n74138_2_pin4),
    .pin6(OEL), .pin7(n74138_2_pin7), .pin15(n74138_2_pin15), .pin14(n74138_2_pin14), .pin13(n74138_2_pin13),
    .pin12(n74138_2_pin12), .pin11(n74138_2_pin11), .pin10(n74138_2_pin10), .pin9(n74138_2_pin9));
  _74138 u_74138_3 (
    .pin1(QSELR[0]), .pin2(QSELR[1]), .pin3(QSELR[2]), .pin4(n74138_3_pin4), .pin5(n74138_3_pin4),
    .pin6(OER), .pin7(n74138_3_pin7), .pin15(n74138_3_pin15), .pin14(n74138_3_pin14), .pin13(n74138_3_pin13),
    .pin12(n74138_3_pin12), .pin11(n74138_3_pin11), .pin10(n74138_3_pin10), .pin9(n74138_3_pin9));
  Reg16Buf2 reg16buf2_1 (
    .CLK(CLK), .nWE(n74138_1_pin15), .D(D), .nOE0(n74138_2_pin15), .nOE1(n74138_3_pin15), .Q0(QL), .Q1(QR),
    .DBG_Q(DBG_R0));
  Reg16Buf2 reg16buf2_2 (
    .CLK(CLK), .nWE(n74138_1_pin14), .D(D), .nOE0(n74138_2_pin14), .nOE1(n74138_3_pin14), .Q0(QL), .Q1(QR),
    .DBG_Q(DBG_R1));
  Reg16Buf2 reg16buf2_3 (
    .CLK(CLK), .nWE(n74138_1_pin13), .D(D), .nOE0(n74138_2_pin13), .nOE1(n74138_3_pin13), .Q0(QL), .Q1(QR),
    .DBG_Q(DBG_R2));
  Reg16Buf2 reg16buf2_4 (
    .CLK(CLK), .nWE(n74138_1_pin12), .D(D), .nOE0(n74138_2_pin12), .nOE1(n74138_3_pin12), .Q0(QL), .Q1(QR),
    .DBG_Q(DBG_R3));
  Reg16Buf2 reg16buf2_5 (
    .CLK(CLK), .nWE(n74138_1_pin11), .D(D), .nOE0(n74138_2_pin11), .nOE1(n74138_3_pin11), .Q0(QL), .Q1(QR),
    .DBG_Q(DBG_R4));
  Reg16Buf2 reg16buf2_6 (
    .CLK(CLK), .nWE(n74138_1_pin10), .D(D), .nOE0(n74138_2_pin10), .nOE1(n74138_3_pin10), .Q0(QL), .Q1(QR),
    .DBG_Q(DBG_R5));
  RegSPBuf2 regspbuf2_1 (
    .CLK(CLK), .nWE(n74138_1_pin9), .D(D), .nOE0(n74138_2_pin9), .nOE1(n74138_3_pin9), .Q0(QL), .Q1(QR),
    .DBG_Q(DBG_R6));
  RegPCBuf2 regpcbuf2_1 (
    .nCLR(nPCCLR), .CLK(CLK), .CNTE(PCCNTE), .nWE(n74138_1_pin7), .D(D), .nOE0(n74138_2_pin7),
    .nOE1(n74138_3_pin7), .PC0(PC0), .QPC(QPC), .Q0(QL), .Q1(QR));
  // also tied to GND on the sheet: {n74138_1_pin4, n74138_2_pin4, n74138_3_pin4}
endmodule

module SelRegFile (
  input  CLK,
  input  [15:0] D,
  input  [2:0] RSEL,
  input  OWE,
  input  OnW,
  input  [2:0] ASEL,
  input  nCLR,
  output [15:0] Q,
  output [7:0] A,
  output [7:0] DBG_SEL0,
  output [7:0] DBG_SEL1,
  output [7:0] DBG_SEL2,
  output [7:0] DBG_SEL3,
  output [7:0] DBG_SEL4,
  output [7:0] DBG_SEL5,
  output [7:0] DBG_SEL6,
  output [7:0] DBG_SEL7
);

  wire n7400_1_pin3, n7400_1_pin4, n74138_1_pin4, n74138_1_pin5, n74138_1_pin6, n74138_1_pin7, n74138_1_pin9,
       n74138_1_pin10, n74138_1_pin11, n74138_1_pin12, n74138_1_pin13, n74138_1_pin14, n74138_1_pin15,
       n74138_2_pin4, n74138_2_pin5, n74138_2_pin6, n74138_2_pin7, n74138_2_pin9, n74138_2_pin10,
       n74138_2_pin11, n74138_2_pin12, n74138_2_pin13, n74138_2_pin14, n74138_2_pin15, n74138_3_pin4,
       n74138_3_pin6, n74138_3_pin7, n74138_3_pin9, n74138_3_pin10, n74138_3_pin11, n74138_3_pin12,
       n74138_3_pin13, n74138_3_pin14, n74138_3_pin15;

  _74138 u_74138_1 (
    .pin1(RSEL[0]), .pin2(RSEL[1]), .pin3(RSEL[2]), .pin4(n74138_1_pin4), .pin5(n74138_1_pin5),
    .pin6(n74138_1_pin6), .pin7(n74138_1_pin7), .pin15(n74138_1_pin15), .pin14(n74138_1_pin14),
    .pin13(n74138_1_pin13), .pin12(n74138_1_pin12), .pin11(n74138_1_pin11), .pin10(n74138_1_pin10),
    .pin9(n74138_1_pin9));
  _74138 u_74138_2 (
    .pin1(RSEL[0]), .pin2(RSEL[1]), .pin3(RSEL[2]), .pin4(n74138_2_pin4), .pin5(n74138_2_pin5),
    .pin6(n74138_2_pin6), .pin7(n74138_2_pin7), .pin15(n74138_2_pin15), .pin14(n74138_2_pin14),
    .pin13(n74138_2_pin13), .pin12(n74138_2_pin12), .pin11(n74138_2_pin11), .pin10(n74138_2_pin10),
    .pin9(n74138_2_pin9));
  _74138 u_74138_3 (
    .pin1(ASEL[0]), .pin2(ASEL[1]), .pin3(ASEL[2]), .pin4(n74138_3_pin4), .pin5(n74138_3_pin4),
    .pin6(n74138_3_pin6), .pin7(n74138_3_pin7), .pin15(n74138_3_pin15), .pin14(n74138_3_pin14),
    .pin13(n74138_3_pin13), .pin12(n74138_3_pin12), .pin11(n74138_3_pin11), .pin10(n74138_3_pin10),
    .pin9(n74138_3_pin9));
  _7400 u_7400_1 (
    .pin1(OnW), .pin2(OnW), .pin3(n7400_1_pin3), .pin4(n7400_1_pin4), .pin5(n7400_1_pin4), .pin13(OnW),
    .pin12(OWE), .pin11(n74138_2_pin5), .pin10(OWE), .pin9(n7400_1_pin3), .pin8(n74138_1_pin5));  // open: pin6
  RegCnt8Buf2 regcnt8buf2_1 (
    .nCLR(nCLR), .CLK(CLK), .nWE(n74138_1_pin15), .D(D[7:0]), .nOE0(n74138_2_pin15), .nOE1(n74138_3_pin15),
    .CNTE(1'b0), .Q0(Q[7:0]), .Q1(A), .DBG_Q(DBG_SEL0));  // open: TC
  Reg8Buf2 reg8buf2_1 (
    .CLK(CLK), .nWE(n74138_1_pin14), .D(D[7:0]), .nOE0(n74138_2_pin14), .nOE1(n74138_3_pin14), .Q0(Q[7:0]),
    .Q1(A), .DBG_Q(DBG_SEL1));
  Reg8Buf2 reg8buf2_2 (
    .CLK(CLK), .nWE(n74138_1_pin13), .D(D[7:0]), .nOE0(n74138_2_pin13), .nOE1(n74138_3_pin13), .Q0(Q[7:0]),
    .Q1(A), .DBG_Q(DBG_SEL2));
  Reg8Buf2 reg8buf2_3 (
    .CLK(CLK), .nWE(n74138_1_pin12), .D(D[7:0]), .nOE0(n74138_2_pin12), .nOE1(n74138_3_pin12), .Q0(Q[7:0]),
    .Q1(A), .DBG_Q(DBG_SEL3));
  RegCnt8Buf2 regcnt8buf2_2 (
    .nCLR(nCLR), .CLK(CLK), .nWE(n74138_1_pin11), .D(D[7:0]), .nOE0(n74138_2_pin11), .nOE1(n74138_3_pin11),
    .CNTE(1'b0), .Q0(Q[7:0]), .Q1(A), .DBG_Q(DBG_SEL4));  // open: TC
  Reg8Buf2 reg8buf2_4 (
    .CLK(CLK), .nWE(n74138_1_pin10), .D(D[7:0]), .nOE0(n74138_2_pin10), .nOE1(n74138_3_pin10), .Q0(Q[7:0]),
    .Q1(A), .DBG_Q(DBG_SEL5));
  Reg8Buf2 reg8buf2_5 (
    .CLK(CLK), .nWE(n74138_1_pin9), .D(D[7:0]), .nOE0(n74138_2_pin9), .nOE1(n74138_3_pin9), .Q0(Q[7:0]),
    .Q1(A), .DBG_Q(DBG_SEL6));
  Reg8Buf2 reg8buf2_6 (
    .CLK(CLK), .nWE(n74138_1_pin7), .D(D[7:0]), .nOE0(n74138_2_pin7), .nOE1(n74138_3_pin7), .Q0(Q[7:0]),
    .Q1(A), .DBG_Q(DBG_SEL7));
  Buf8 buf8_1 (.DI({8{1'b0}}), .nOE(n74138_2_pin5), .DO(Q[15:8]));
  // also tied to GND on the sheet: {n74138_1_pin4, n74138_2_pin4, n74138_3_pin4, n7400_1_pin4}
  // also tied to VCC on the sheet: {n74138_3_pin6, n74138_1_pin6, n74138_2_pin6}
endmodule

module RamProt (
  input  OEI,
  input  WEI,
  input  A0,
  input  W16,
  output OEO,
  output WEO
);

  wire n7400_1_pin3, n7400_1_pin6, n7400_1_pin11, n7400_1_pin12, n7400_2_pin3, n7400_2_pin11;

  _7400 u_7400_1 (
    .pin1(OEI), .pin2(WEI), .pin3(n7400_1_pin3), .pin4(A0), .pin5(W16), .pin6(n7400_1_pin6), .pin13(OEI),
    .pin12(n7400_1_pin12), .pin11(n7400_1_pin11), .pin10(n7400_1_pin11), .pin9(n7400_1_pin11), .pin8(OEO));
  _7400 u_7400_2 (
    .pin1(WEI), .pin2(n7400_1_pin12), .pin3(n7400_2_pin3), .pin4(n7400_2_pin3), .pin5(n7400_2_pin3),
    .pin6(WEO), .pin13(n7400_1_pin6), .pin12(n7400_1_pin3), .pin11(n7400_2_pin11), .pin10(n7400_2_pin11),
    .pin9(n7400_2_pin11), .pin8(n7400_1_pin12));

  // Notes on the sheet:
  //   OE=WE=1 Protect
  //   A0=W16=1 Protect
endmodule

module Ram8_16 (
  input  [15:0] A,
  input  CLK,
  input  [15:0] DI,
  input  OE,
  input  WE,
  input  W16,
  output [15:0] DO
);

  wire n7400_1_pin1, n7400_1_pin6, n7400_1_pin11, n7400_1_pin13, n7400_2_pin1, n7400_2_pin2, n7400_2_pin3,
       n7400_2_pin6, n7400_3_pin3, n7400_3_pin6, n7400_3_pin8, n7400_3_pin11, ramprot_1_oeo, ramprot_1_weo;
  wire [7:0] ram_1_data, ram_2_data;

  RamProt ramprot_1 (.OEI(OE), .WEI(WE), .A0(A[0]), .W16(W16), .OEO(ramprot_1_oeo), .WEO(ramprot_1_weo));
  RAM #(.addrWidth(15), .asyncread("true"), .databus("bidir")) ram_1 (
    .addr(A[15:1]), .we(n7400_1_pin11), .oe(ramprot_1_oeo), .clk(CLK), .data(ram_1_data));
  RAM #(.addrWidth(15), .asyncread("true"), .databus("bidir")) ram_2 (
    .addr(A[15:1]), .we(n7400_2_pin3), .oe(ramprot_1_oeo), .clk(CLK), .data(ram_2_data));
  _7400 u_7400_1 (
    .pin1(n7400_1_pin1), .pin2(n7400_1_pin1), .pin4(A[0]), .pin5(A[0]), .pin6(n7400_1_pin6),
    .pin13(n7400_1_pin13), .pin12(n7400_1_pin13), .pin11(n7400_1_pin11), .pin10(n7400_1_pin6),
    .pin9(ramprot_1_weo), .pin8(n7400_1_pin13));  // open: pin3
  Buf8 buf8_1 (.DI(DI[7:0]), .nOE(n7400_1_pin13), .DO(ram_1_data));
  _7400 u_7400_2 (
    .pin1(n7400_2_pin1), .pin2(n7400_2_pin2), .pin3(n7400_2_pin3), .pin4(n7400_1_pin6), .pin5(ramprot_1_oeo),
    .pin6(n7400_2_pin6), .pin13(A[0]), .pin12(ramprot_1_weo), .pin11(n7400_2_pin1), .pin10(W16),
    .pin9(ramprot_1_weo), .pin8(n7400_2_pin2));
  Buf8 buf8_2 (.DI(DI[7:0]), .nOE(n7400_2_pin1), .DO(ram_2_data));
  Buf8 buf8_3 (.DI(DI[15:8]), .nOE(n7400_2_pin2), .DO(ram_2_data));
  Buf8 buf8_4 (.DI(ram_1_data), .nOE(n7400_2_pin6), .DO(DI[7:0]));
  Buf8 buf8_5 (.DI(ram_2_data), .nOE(n7400_3_pin3), .DO(DI[7:0]));
  _7400 u_7400_3 (
    .pin1(A[0]), .pin2(ramprot_1_oeo), .pin3(n7400_3_pin3), .pin4(W16), .pin5(W16), .pin6(n7400_3_pin6),
    .pin13(W16), .pin12(ramprot_1_oeo), .pin11(n7400_3_pin11), .pin10(ramprot_1_oeo), .pin9(n7400_3_pin6),
    .pin8(n7400_3_pin8));
  Buf8 buf8_6 (.DI(ram_2_data), .nOE(n7400_3_pin11), .DO(DI[15:8]));
  Buf8 buf8_7 (.DI({8{1'b0}}), .nOE(n7400_3_pin8), .DO(DI[15:8]));

  assign DO = DI;
  // also tied to GND on the sheet: n7400_1_pin1

  // Notes on the sheet:
  //   OE=WE=1 Protect
  //   A0=W16=1 Protect
  //   EvenBytes
  //   OddBytes
  //   OE
  //   EvenWE
  //   WE
  //   OddWE
  //   A0
  //   W16
  //   WriteEvenLo
  //   WriteOddLo
  //   WriteOddHi
  //   ReadEvenLo
  //   ReadOddLo
  //   ReadOddHi
  //   ReadZeroExt
endmodule

module MemIf8_16 (
  input  [7:0] EvenDI,
  input  [7:0] OddDI,
  input  [15:0] AI,
  input  [15:0] DI,
  input  OE,
  input  WE,
  input  W16,
  output [14:0] AO,
  output [7:0] EvenDO,
  output [7:0] OddDO,
  output [15:0] DO,
  output BothOE,
  output EvenWE,
  output OddWE
);

  wire n7400_1_pin1, n7400_1_pin6, n7400_1_pin13, n7400_2_pin1, n7400_2_pin2, n7400_2_pin6, n7400_3_pin3,
       n7400_3_pin6, n7400_3_pin8, n7400_3_pin11, ramprot_1_weo;

  RamProt ramprot_1 (.OEI(OE), .WEI(WE), .A0(AI[0]), .W16(W16), .OEO(BothOE), .WEO(ramprot_1_weo));
  _7400 u_7400_1 (
    .pin1(n7400_1_pin1), .pin2(n7400_1_pin1), .pin4(AI[0]), .pin5(AI[0]), .pin6(n7400_1_pin6),
    .pin13(n7400_1_pin13), .pin12(n7400_1_pin13), .pin11(EvenWE), .pin10(n7400_1_pin6), .pin9(ramprot_1_weo),
    .pin8(n7400_1_pin13));  // open: pin3
  Buf8 buf8_1 (.DI(DI[7:0]), .nOE(n7400_1_pin13), .DO(EvenDO));
  Buf8 buf8_2 (.DI(DI[7:0]), .nOE(n7400_2_pin1), .DO(OddDO));
  _7400 u_7400_2 (
    .pin1(n7400_2_pin1), .pin2(n7400_2_pin2), .pin3(OddWE), .pin4(n7400_1_pin6), .pin5(BothOE),
    .pin6(n7400_2_pin6), .pin13(AI[0]), .pin12(ramprot_1_weo), .pin11(n7400_2_pin1), .pin10(W16),
    .pin9(ramprot_1_weo), .pin8(n7400_2_pin2));
  Buf8 buf8_3 (.DI(DI[15:8]), .nOE(n7400_2_pin2), .DO(OddDO));
  Buf8 buf8_4 (.DI(EvenDI), .nOE(n7400_2_pin6), .DO(DI[7:0]));
  Buf8 buf8_5 (.DI(OddDI), .nOE(n7400_3_pin3), .DO(DI[7:0]));
  _7400 u_7400_3 (
    .pin1(AI[0]), .pin2(BothOE), .pin3(n7400_3_pin3), .pin4(W16), .pin5(W16), .pin6(n7400_3_pin6),
    .pin13(W16), .pin12(BothOE), .pin11(n7400_3_pin11), .pin10(BothOE), .pin9(n7400_3_pin6),
    .pin8(n7400_3_pin8));
  Buf8 buf8_6 (.DI(OddDI), .nOE(n7400_3_pin11), .DO(DI[15:8]));
  Buf8 buf8_7 (.DI({8{1'b0}}), .nOE(n7400_3_pin8), .DO(DI[15:8]));

  assign AO = AI[15:1];
  assign DO = DI;
  // also tied to GND on the sheet: n7400_1_pin1

  // Notes on the sheet:
  //   For 2 8-bit RAMs
  //   OE=WE=1 Protect
  //   A0=W16=1 Protect
  //   EvenWE
  //   WriteEvenLo
  //   WriteOddLo
  //   OddWE
  //   WriteOddHi
  //   ReadEvenLo
  //   ReadOddLo
  //   ReadOddHi
  //   ReadZeroExt
endmodule

module MemIf8_16w (
  input  [15:0] MDI,
  input  [21:0] AI,
  input  [15:0] DI,
  input  OE,
  input  WE,
  input  W16,
  output [20:0] AO,
  output [15:0] MDO,
  output [15:0] DO,
  output BothOE,
  output BothWE,
  output EvenE,
  output OddE
);

  wire n7400_1_pin1, n7400_1_pin8, n7400_2_pin1, n7400_2_pin6, n7400_2_pin8, n7400_2_pin11, n7400_3_pin3,
       n7400_3_pin8, n7400_3_pin11;

  RamProt ramprot_1 (.OEI(OE), .WEI(WE), .A0(AI[0]), .W16(W16), .OEO(BothOE), .WEO(BothWE));
  _7400 u_7400_1 (
    .pin1(n7400_1_pin1), .pin2(n7400_1_pin1), .pin4(AI[0]), .pin5(AI[0]), .pin6(EvenE), .pin13(n7400_1_pin1),
    .pin12(n7400_1_pin1), .pin10(BothWE), .pin9(BothWE), .pin8(n7400_1_pin8));  // open: pin3, pin11
  Buf8 buf8_1 (.DI(DI[7:0]), .nOE(n7400_1_pin8), .DO(MDO[7:0]));
  Buf8 buf8_2 (.DI(DI[7:0]), .nOE(n7400_2_pin11), .DO(MDO[15:8]));
  _7400 u_7400_2 (
    .pin1(n7400_2_pin1), .pin2(EvenE), .pin3(OddE), .pin4(EvenE), .pin5(BothOE), .pin6(n7400_2_pin6),
    .pin13(AI[0]), .pin12(BothWE), .pin11(n7400_2_pin11), .pin10(EvenE), .pin9(BothWE), .pin8(n7400_2_pin8));
  Buf8 buf8_3 (.DI(DI[15:8]), .nOE(n7400_2_pin8), .DO(MDO[15:8]));
  Buf8 buf8_4 (.DI(MDI[7:0]), .nOE(n7400_2_pin6), .DO(DI[7:0]));
  Buf8 buf8_5 (.DI(MDI[15:8]), .nOE(n7400_3_pin3), .DO(DI[7:0]));
  _7400 u_7400_3 (
    .pin1(AI[0]), .pin2(BothOE), .pin3(n7400_3_pin3), .pin4(W16), .pin5(W16), .pin6(n7400_2_pin1),
    .pin13(W16), .pin12(BothOE), .pin11(n7400_3_pin11), .pin10(BothOE), .pin9(n7400_2_pin1),
    .pin8(n7400_3_pin8));
  Buf8 buf8_6 (.DI(MDI[15:8]), .nOE(n7400_3_pin11), .DO(DI[15:8]));
  Buf8 buf8_7 (.DI({8{1'b0}}), .nOE(n7400_3_pin8), .DO(DI[15:8]));

  assign AO = AI[21:1];
  assign DO = DI;
  // also tied to GND on the sheet: n7400_1_pin1

  // Notes on the sheet:
  //   For 16-bit RAM with byte/word R/W
  //   WriteEvenLo
  //   WriteOddLo
  //   WriteOddHi
  //   ReadEvenLo
  //   ReadOddLo
  //   ReadOddHi
  //   ReadZeroExt
endmodule

module MemIf8_16RxM (
  input  [15:0] RAMDI,
  input  [15:0] ROMDI,
  input  [21:0] AI,
  input  [15:0] DI,
  input  OE,
  input  WE,
  input  W16,
  output [20:0] AO,
  output [15:0] RAMDO,
  output [15:0] DO,
  output BothOE,
  output BothWE,
  output EvenE,
  output OddE
);

  wire n7400_1_pin1, n7400_1_pin8, n7400_1_pin11, n7400_1_pin13, n7400_2_pin1, n7400_2_pin6, n7400_2_pin8,
       n7400_2_pin11, n7400_3_pin3, n7400_3_pin8, n7400_3_pin11, n7411_1_pin1, n7427_1_pin6, n7427_1_pin8,
       n7427_1_pin12, ramprot_1_weo;
  wire [15:0] sel16_1_do;

  RamProt ramprot_1 (.OEI(OE), .WEI(WE), .A0(AI[0]), .W16(W16), .OEO(BothOE), .WEO(ramprot_1_weo));
  _7427 u_7427_1 (
    .pin1(AI[20]), .pin2(AI[19]), .pin3(AI[18]), .pin4(AI[17]), .pin5(AI[16]), .pin6(n7427_1_pin6),
    .pin13(AI[21]), .pin12(n7427_1_pin12), .pin11(AI[15]), .pin10(AI[14]), .pin9(AI[14]), .pin8(n7427_1_pin8));
  _7400 u_7400_1 (
    .pin1(n7400_1_pin1), .pin2(n7400_1_pin1), .pin4(AI[0]), .pin5(AI[0]), .pin6(EvenE),
    .pin13(n7400_1_pin13), .pin12(n7400_1_pin13), .pin11(n7400_1_pin11), .pin10(BothWE), .pin9(BothWE),
    .pin8(n7400_1_pin8));  // open: pin3
  _7411 u_7411_1 (
    .pin1(n7411_1_pin1), .pin2(n7411_1_pin1), .pin3(n7427_1_pin12), .pin4(n7427_1_pin8), .pin5(n7427_1_pin6),
    .pin6(n7400_1_pin13), .pin13(n7411_1_pin1), .pin11(ramprot_1_weo), .pin10(ramprot_1_weo),
    .pin9(n7400_1_pin11), .pin8(BothWE));  // open: pin12
  Buf8 buf8_1 (.DI(DI[7:0]), .nOE(n7400_1_pin8), .DO(RAMDO[7:0]));
  Buf8 buf8_2 (.DI(DI[7:0]), .nOE(n7400_2_pin11), .DO(RAMDO[15:8]));
  _7400 u_7400_2 (
    .pin1(n7400_2_pin1), .pin2(EvenE), .pin3(OddE), .pin4(EvenE), .pin5(BothOE), .pin6(n7400_2_pin6),
    .pin13(AI[0]), .pin12(BothWE), .pin11(n7400_2_pin11), .pin10(EvenE), .pin9(BothWE), .pin8(n7400_2_pin8));
  Buf8 buf8_3 (.DI(DI[15:8]), .nOE(n7400_2_pin8), .DO(RAMDO[15:8]));
  Buf8 buf8_4 (.DI(sel16_1_do[7:0]), .nOE(n7400_2_pin6), .DO(DI[7:0]));
  Buf8 buf8_5 (.DI(sel16_1_do[15:8]), .nOE(n7400_3_pin3), .DO(DI[7:0]));
  _7400 u_7400_3 (
    .pin1(AI[0]), .pin2(BothOE), .pin3(n7400_3_pin3), .pin4(W16), .pin5(W16), .pin6(n7400_2_pin1),
    .pin13(W16), .pin12(BothOE), .pin11(n7400_3_pin11), .pin10(BothOE), .pin9(n7400_2_pin1),
    .pin8(n7400_3_pin8));
  Buf8 buf8_6 (.DI(sel16_1_do[15:8]), .nOE(n7400_3_pin11), .DO(DI[15:8]));
  Buf8 buf8_7 (.DI({8{1'b0}}), .nOE(n7400_3_pin8), .DO(DI[15:8]));
  Sel16 sel16_1 (.DI0(RAMDI), .DI1(ROMDI), .SEL(n7400_1_pin13), .DO(sel16_1_do));

  assign AO = AI[21:1];
  assign DO = DI;
  // also tied to GND on the sheet: {n7400_1_pin1, n7411_1_pin1}

  // Notes on the sheet:
  //   For 16-bit RAM with byte/word R/W and 16-bit ROM
  //   WriteEvenLo
  //   WriteOddLo
  //   WriteOddHi
  //   ReadEvenLo
  //   ReadOddLo
  //   ReadOddHi
  //   ReadZeroExt
endmodule

module ImmDecoder (
  input  [15:0] INSTR,
  input  [2:0] SEL,
  input  nOE,
  input  CONDVAL,
  output [15:0] IMM
);

  wire n74138_1_pin5, n74138_1_pin6, n74138_1_pin7, n74138_1_pin9, n74138_1_pin10, n74138_1_pin11,
       n74138_1_pin12, n74138_1_pin13, n74138_1_pin14, n74138_1_pin15;
  wire [7:7] sel8_1_do_2;
  wire [15:1] sel8_1_do;

  _74138 u_74138_1 (
    .pin1(SEL[0]), .pin2(SEL[1]), .pin3(SEL[2]), .pin4(nOE), .pin5(n74138_1_pin5), .pin6(n74138_1_pin6),
    .pin7(n74138_1_pin7), .pin15(n74138_1_pin15), .pin14(n74138_1_pin14), .pin13(n74138_1_pin13),
    .pin12(n74138_1_pin12), .pin11(n74138_1_pin11), .pin10(n74138_1_pin10), .pin9(n74138_1_pin9));
  Sel8 sel8_1 (
    .DI0({8{1'b0}}), .DI1({{2{INSTR[12]}}, INSTR[11:6]}), .SEL(CONDVAL),
    .DO({sel8_1_do_2[7], sel8_1_do[15], sel8_1_do[6:1]}));
  Buf16 buf16_1 (.DI({{9{1'b0}}, INSTR[6:0]}), .nOE(n74138_1_pin14), .DO(IMM));
  Buf16 buf16_2 (.DI({{10{INSTR[6]}}, INSTR[5:0]}), .nOE(n74138_1_pin13), .DO(IMM));
  Buf16 buf16_3 (.DI({{9{sel8_1_do[15]}}, sel8_1_do[6:1], 1'b0}), .nOE(n74138_1_pin12), .DO(IMM));
  Buf16 buf16_4 (.DI({INSTR[9:1], {7{1'b0}}}), .nOE(n74138_1_pin11), .DO(IMM));
  Buf16 buf16_5 (.DI({{8{INSTR[9]}}, INSTR[8:1]}), .nOE(n74138_1_pin10), .DO(IMM));
  Buf16 buf16_6 (.DI({{5{INSTR[10]}}, INSTR[9:0], 1'b0}), .nOE(n74138_1_pin9), .DO(IMM));
  Buf16 buf16_7 (.DI({16{1'b1}}), .nOE(n74138_1_pin15), .DO(IMM));
  Buf16 buf16_8 (.DI(16'hfffe), .nOE(n74138_1_pin7), .DO(IMM));
  // also tied to GND on the sheet: n74138_1_pin5
  // also tied to VCC on the sheet: n74138_1_pin6

  // Notes on the sheet:
  //   1: imm7
  //   2: simm7
  //   4: imm9<<7
  //   5: simm9
  //   6: simm11<<1
  //   0: -1 for cpl (reg XOR -1)
  //   7: -2 for sp-2
  //   3: simm7<<1 (cond jump)
endmodule

module InstrCompressor (
  input  [15:0] INSTRI,
  output [7:0] INSTRO
);

  wire n7410_1_pin3, n7410_1_pin12;

  _7410 u_7410_1 (
    .pin1(INSTRI[14]), .pin2(INSTRI[15]), .pin3(n7410_1_pin3), .pin4(n7410_1_pin3), .pin5(n7410_1_pin3),
    .pin13(INSTRI[13]), .pin12(n7410_1_pin12), .pin11(n7410_1_pin3), .pin10(n7410_1_pin3), .pin9(n7410_1_pin3));  // open: pin6, pin8
  Sel8 sel8_1 (.DI0({1'b1, INSTRI[6:0]}), .DI1({1'b0, INSTRI[15:10], INSTRI[0]}), .SEL(n7410_1_pin12), .DO(INSTRO));
  // also tied to GND on the sheet: n7410_1_pin3

  // Notes on the sheet:
  //   NNNrrrRRRo##oooo => 1o##oooo, NNN=111
  //   NNNrrrxxxxxxxxxL => 0NNNrrrL, NNN!=111
endmodule

module Shifter16 (
  input  [15:0] DI,
  input  LEFT,
  input  SEXT,
  input  ROT,
  input  [15:0] CNT,
  output [15:0] DO
);

  wire n7400_1_pin3, n7400_1_pin13;
  wire [0:0] bitrev16_1_do_2, sel4_1_do;
  wire [3:0] sel4_2_do;
  wire [3:3] n7400_1_pin6;
  wire [7:0] sel8_1_do, sel16_3_do, sel16_3_do_2;
  wire [15:0] bitrev16_1_do, sel16_1_do, sel16_2_do, sel16_4_do;
  wire [15:14] sel4_1_do_2;

  BitRev16 bitrev16_1 (.DI(DI), .REV(LEFT), .DO({bitrev16_1_do[14:0], bitrev16_1_do_2[0]}));
  Sel16 sel16_1 (.DI0({bitrev16_1_do[14:0], bitrev16_1_do_2[0]}), .DI1(bitrev16_1_do), .SEL(CNT[0]), .DO(sel16_1_do));
  Sel16 sel16_2 (.DI0(sel16_1_do), .DI1({sel4_1_do_2, sel16_1_do[15:2]}), .SEL(CNT[1]), .DO(sel16_2_do));
  Sel16 sel16_3 (.DI0(sel16_2_do), .DI1({sel4_2_do, sel16_2_do[15:4]}), .SEL(CNT[2]), .DO({sel16_3_do, sel16_3_do_2}));
  Sel16 sel16_4 (.DI0({sel16_3_do, sel16_3_do_2}), .DI1({sel8_1_do, sel16_3_do}), .SEL(CNT[3]), .DO(sel16_4_do));
  BitRev16 bitrev16_2 (.DI(sel16_4_do), .REV(LEFT), .DO(DO));
  _7400 u_7400_1 (
    .pin1(bitrev16_1_do[14]), .pin2(SEXT), .pin3(n7400_1_pin3), .pin4(n7400_1_pin3), .pin5(n7400_1_pin3),
    .pin6(n7400_1_pin6[3]), .pin13(n7400_1_pin13), .pin12(n7400_1_pin13), .pin10(n7400_1_pin13),
    .pin9(n7400_1_pin13));  // open: pin11, pin8
  Sel4 sel4_1 (
    .DI0({4{n7400_1_pin6[3]}}), .DI1({sel16_1_do[1:0], bitrev16_1_do_2[0], 1'b0}), .SEL(ROT),
    .DO({sel4_1_do_2, bitrev16_1_do[15], sel4_1_do[0]}));
  Sel4 sel4_2 (.DI0({4{n7400_1_pin6[3]}}), .DI1(sel16_2_do[3:0]), .SEL(ROT), .DO(sel4_2_do));
  Sel8 sel8_1 (.DI0({8{n7400_1_pin6[3]}}), .DI1(sel16_3_do_2), .SEL(ROT), .DO(sel8_1_do));
  // also tied to GND on the sheet: n7400_1_pin13

  // Notes on the sheet:
  //   <<1
  //   <<2
  //   <<4
  //   <<8
  //   sign or zero
endmodule

module Adder16 (
  input  [15:0] DI0,
  input  [15:0] DI1,
  input  CI,
  input  SUB,
  output [15:0] DO,
  output CO,
  output OVF
);

  wire add16_1_co, n7486_1_pin1, n7486_1_pin8, n7486_2_pin3, n7486_2_pin5;
  wire [15:0] xor16_1_do;

  _7486 u_7486_1 (
    .pin1(n7486_1_pin1), .pin2(n7486_1_pin1), .pin4(n7486_1_pin1), .pin5(n7486_1_pin1), .pin13(n7486_1_pin1),
    .pin12(n7486_1_pin1), .pin10(SUB), .pin9(CI), .pin8(n7486_1_pin8));  // open: pin3, pin6, pin11
  Add16 add16_1 (.DI0(DI0), .DI1(xor16_1_do), .CI(n7486_1_pin8), .DO(DO), .CO(add16_1_co));
  Xor16 xor16_1 (.DI0(DI1), .DI1({16{SUB}}), .DO(xor16_1_do));
  _7486 u_7486_2 (
    .pin1(xor16_1_do[15]), .pin2(DI0[15]), .pin3(n7486_2_pin3), .pin4(n7486_2_pin3), .pin5(n7486_2_pin5),
    .pin6(OVF), .pin13(DO[15]), .pin12(add16_1_co), .pin11(n7486_2_pin5), .pin10(SUB), .pin9(add16_1_co),
    .pin8(CO));
  // also tied to GND on the sheet: n7486_1_pin1
endmodule

module ZeroDetector16 (
  input  [15:0] D,
  output Z,
  output S
);

  wire n7411_1_pin3, n7411_1_pin4, n7411_1_pin9, n7411_1_pin10, n7411_1_pin11, n7427_1_pin6, n7427_1_pin8,
       n7427_1_pin12;

  _7427 u_7427_1 (
    .pin1(D[12]), .pin2(D[13]), .pin3(D[14]), .pin4(D[15]), .pin5(D[15]), .pin6(n7427_1_pin6), .pin13(D[11]),
    .pin12(n7427_1_pin12), .pin11(D[10]), .pin10(D[9]), .pin9(D[8]), .pin8(n7427_1_pin8));
  _7411 u_7411_1 (
    .pin1(n7427_1_pin8), .pin2(n7427_1_pin6), .pin3(n7411_1_pin3), .pin4(n7411_1_pin4), .pin5(n7411_1_pin4),
    .pin6(Z), .pin13(n7427_1_pin12), .pin12(n7411_1_pin3), .pin11(n7411_1_pin11), .pin10(n7411_1_pin10),
    .pin9(n7411_1_pin9), .pin8(n7411_1_pin4));
  _7427 u_7427_2 (
    .pin1(D[3]), .pin2(D[4]), .pin3(D[5]), .pin4(D[6]), .pin5(D[7]), .pin6(n7411_1_pin9), .pin13(D[2]),
    .pin12(n7411_1_pin11), .pin11(D[1]), .pin10(D[0]), .pin9(D[0]), .pin8(n7411_1_pin10));

  assign S = D[15];
endmodule

module ALU (
  input  [15:0] DIL,
  input  [15:0] DIR,
  input  [3:0] OP,
  input  CI,
  output [15:0] DO,
  output CO,
  output Z,
  output S,
  output OVF
);

  wire n7400_1_pin6, n7400_1_pin8, n7404_1_pin1, n7404_1_pin2, n7404_1_pin3, n7404_1_pin4, n7404_1_pin6,
       n7404_1_pin8, n7404_1_pin10, n7404_1_pin12, n7410_1_pin6, n7410_1_pin8, n7410_1_pin12, n7410_2_pin6,
       n7410_2_pin12;
  wire [1:0] adder16_1_co;
  wire [3:2] sel4_1_do;
  wire [15:0] adder16_1_do, and16_1_do, or16_1_do, shifter16_1_do, xor16_1_do;
  wire [15:15] n7410_2_pin8;

  _7404 u_7404_1 (
    .pin1(n7404_1_pin1), .pin2(n7404_1_pin2), .pin3(n7404_1_pin3), .pin4(n7404_1_pin4), .pin5(OP[3]),
    .pin6(n7404_1_pin6), .pin13(OP[0]), .pin12(n7404_1_pin12), .pin11(OP[1]), .pin10(n7404_1_pin10),
    .pin9(OP[2]), .pin8(n7404_1_pin8));
  _7400 u_7400_1 (
    .pin1(CI), .pin2(OP[1]), .pin3(n7404_1_pin1), .pin4(OP[3]), .pin5(n7404_1_pin8), .pin6(n7400_1_pin6),
    .pin13(OP[2]), .pin12(OP[1]), .pin11(n7404_1_pin3), .pin10(n7404_1_pin3), .pin9(n7404_1_pin6),
    .pin8(n7400_1_pin8));
  Shifter16 shifter16_1 (.DI(DIL), .LEFT(OP[0]), .SEXT(OP[2]), .ROT(OP[1]), .CNT(DIR), .DO(shifter16_1_do));
  Adder16 adder16_1 (
    .DI0(DIL), .DI1(DIR), .CI(n7404_1_pin2), .SUB(OP[0]), .DO(adder16_1_do), .CO(adder16_1_co[0]),
    .OVF(adder16_1_co[1]));
  Xor16 xor16_1 (.DI0(DIL), .DI1(DIR), .DO(xor16_1_do));
  Or16 or16_1 (.DI0(DIL), .DI1(DIR), .DO(or16_1_do));
  And16 and16_1 (.DI0(DIL), .DI1(DIR), .DO(and16_1_do));
  _7410 u_7410_1 (
    .pin1(OP[0]), .pin2(n7404_1_pin6), .pin3(n7404_1_pin4), .pin4(OP[3]), .pin5(n7404_1_pin12),
    .pin6(n7410_1_pin6), .pin13(n7404_1_pin4), .pin12(n7410_1_pin12), .pin11(n7404_1_pin4), .pin10(OP[3]),
    .pin9(OP[0]), .pin8(n7410_1_pin8));
  _7410 u_7410_2 (
    .pin1(OP[0]), .pin2(OP[0]), .pin3(OP[2]), .pin4(OP[3]), .pin5(n7404_1_pin10), .pin6(n7410_2_pin6),
    .pin13(DIL[7]), .pin12(n7410_2_pin12), .pin11(n7410_2_pin12), .pin10(n7410_2_pin12),
    .pin9(n7410_2_pin12), .pin8(n7410_2_pin8[15]));
  Buf16 buf16_1 (.DI(shifter16_1_do), .nOE(n7400_1_pin8), .DO(DO));
  Buf16 buf16_2 (.DI(adder16_1_do), .nOE(n7400_1_pin6), .DO(DO));
  Buf16 buf16_3 (.DI(xor16_1_do), .nOE(n7410_1_pin12), .DO(DO));
  Buf16 buf16_4 (.DI(or16_1_do), .nOE(n7410_1_pin8), .DO(DO));
  Buf16 buf16_5 (.DI(and16_1_do), .nOE(n7410_1_pin6), .DO(DO));
  Sel4 sel4_1 (.DI0({2'b00, adder16_1_co}), .DI1(4'b0000), .SEL(n7400_1_pin6), .DO({sel4_1_do, OVF, CO}));
  Buf16 buf16_6 (.DI({{8{n7410_2_pin8[15]}}, DIL[7:0]}), .nOE(n7410_2_pin6), .DO(DO));
  ZeroDetector16 zerodetector16_1 (.D(DO), .Z(Z), .S(S));

  // Notes on the sheet:
  //   0: sr
  //   1: sl
  //   2: rr
  //   3: rl
  //   4: asr
  //   5: reserved
  //   6: reserved
  //   7: xor
  //   8: add
  //   9: sub/cmp
  //   10: adc
  //   11: sbb
  //   12: zxt
  //   13: sxt
  //   14: and
  //   15: or
  //   Use 74381s+74382s+74182s for ADD/ADC/SUB/SBB/AND/OR/XOR
endmodule

module CondDecoder (
  input  [15:0] INSTR,
  output [3:0] CONDCODE
);


  assign CONDCODE = INSTR[3:0];
endmodule

module CondEval (
  input  C,
  input  Z,
  input  S,
  input  O,
  input  [3:0] CONDCODE,
  output CONDVAL
);

  wire n7432_1_pin13, n7486_1_pin5, n7486_1_pin9;
  wire [7:3] n7432_1_pin3;

  _7432 u_7432_1 (
    .pin1(C), .pin2(Z), .pin3(n7432_1_pin3[3]), .pin4(Z), .pin5(n7432_1_pin3[4]), .pin6(n7432_1_pin3[5]),
    .pin13(n7432_1_pin13), .pin12(n7432_1_pin13), .pin10(n7432_1_pin13), .pin9(n7432_1_pin13));  // open: pin11, pin8
  _7486 u_7486_1 (
    .pin1(S), .pin2(O), .pin3(n7432_1_pin3[4]), .pin4(O), .pin5(n7486_1_pin5), .pin6(n7432_1_pin3[7]),
    .pin13(n7432_1_pin13), .pin12(n7432_1_pin13), .pin10(CONDCODE[3]), .pin9(n7486_1_pin9), .pin8(CONDVAL));  // open: pin11
  Sel1of8 sel1of8_1 (.DI({n7432_1_pin3[7], O, n7432_1_pin3[5:3], S, Z, C}), .SEL(CONDCODE[2:0]), .DO(n7486_1_pin9));
  // also tied to GND on the sheet: n7432_1_pin13
  // also tied to VCC on the sheet: n7486_1_pin5

  // Notes on the sheet:
  //   1: Z/E
  //   2: S
  //   4: L
  //   5: LE
  //   6: O
  //   7: NO
  //   10: NS
  //   11: GU
  //   12: GE
  //   13: G
  //   0: C/LU
  //   3: LEU
  //   8: NC/GEU
  //   9: NZ/NE
endmodule

module MiscIntMem (
  input  CLK,
  input  nCLR,
  input  D0,
  input  WE0,
  input  D1,
  input  DEL1,
  output Q0,
  output Q1
);

  wire n7474_1_pin4, n7474_1_pin9, sel1_1_do;

  Sel1 sel1_1 (.DI0(Q0), .DI1(D0), .SEL(WE0), .DO(sel1_1_do));
  _7474 u_7474_1 (
    .pin1(nCLR), .pin2(sel1_1_do), .pin3(CLK), .pin4(n7474_1_pin4), .pin5(Q0), .pin13(nCLR), .pin12(D1),
    .pin11(CLK), .pin10(n7474_1_pin4), .pin9(n7474_1_pin9));  // open: pin6, pin8
  Sel1 sel1_2 (.DI0(D1), .DI1(n7474_1_pin9), .SEL(DEL1), .DO(Q1));
  // also tied to VCC on the sheet: n7474_1_pin4

  // Notes on the sheet:
  //   TBD: better name for this special circuit.
endmodule

module RegDecoder (
  input  [2:0] RI,
  input  [2:0] rrr,
  input  [2:0] RRRR,
  output [2:0] RO
);

  wire n7402_1_pin1, n7402_1_pin5;
  wire [3:0] sel4_1_do;

  _7402 #(.ShowInternalStructure("true")) u_7402_1 (
    .pin1(n7402_1_pin1), .pin2(RI[2]), .pin3(RI[1]), .pin5(n7402_1_pin5), .pin6(n7402_1_pin5),
    .pin12(n7402_1_pin5), .pin11(n7402_1_pin5), .pin9(n7402_1_pin5), .pin8(n7402_1_pin5));  // open: pin4, pin13, pin10
  Sel4 sel4_1 (.DI0({{2{rrr[2]}}, rrr[1:0]}), .DI1({{2{RRRR[2]}}, RRRR[1:0]}), .SEL(RI[0]), .DO(sel4_1_do));
  Sel4 sel4_2 (.DI0({{2{RI[2]}}, RI[1:0]}), .DI1(sel4_1_do), .SEL(n7402_1_pin1), .DO({{2{RO[2]}}, RO[1:0]}));
  // also tied to GND on the sheet: n7402_1_pin5
endmodule

module CtrlDecoder (
  input  [31:0] DROM,
  input  FETCHCYCLE,
  input  [15:0] INSTR,
  output [3:0] OP,
  output [2:0] RL,
  output RLOE,
  output [2:0] RR,
  output RROE,
  output [2:0] RI,
  output RIWE,
  output [2:0] IMM,
  output RRBUSOE,
  output ALUOE,
  output FLAGSOE,
  output FLAGSWE,
  output IADDRSEL,
  output IWE,
  output SELE,
  output SELIFLAGSSEL,
  output CNZ,
  output MWE,
  output MOE,
  output W16,
  output CRST
);

  wire [14:4] sel16_1_do;

  Sel16 sel16_1 (
    .DI0(DROM[15:0]), .DI1(16'he8), .SEL(FETCHCYCLE),
    .DO({RIWE, sel16_1_do[14:12], RROE, sel16_1_do[10:8], RLOE, sel16_1_do[6:4], OP}));
  Sel16 sel16_2 (
    .DI0(DROM[31:16]), .DI1(16'h6007), .SEL(FETCHCYCLE),
    .DO({CRST, W16, MOE, MWE, CNZ, SELIFLAGSSEL, SELE, IWE, IADDRSEL, FLAGSWE, FLAGSOE, ALUOE, RRBUSOE, IMM}));
  RegDecoder regdecoder_1 (.RI(sel16_1_do[6:4]), .rrr(INSTR[12:10]), .RRRR(INSTR[9:7]), .RO(RL));
  RegDecoder regdecoder_2 (.RI(sel16_1_do[10:8]), .rrr(INSTR[12:10]), .RRRR(INSTR[9:7]), .RO(RR));
  RegDecoder regdecoder_3 (.RI(sel16_1_do[14:12]), .rrr(INSTR[12:10]), .RRRR(INSTR[9:7]), .RO(RI));

  // Notes on the sheet:
  //   OP_0
  //   OP_1
  //   OP_2
  //   OP_3
  //   RL_0
  //   RL_1
  //   RL_2
  //   RLOE
  //   RR_0
  //   RR_1
  //   RR_2
  //   RROE
  //   RI_0
  //   RI_1
  //   RI_2
  //   RIWE
  //   IMM_0
  //   IMM_1
  //   IMM_2
  //   RRBUSOE
  //   ALUOE
  //   FLAGSOE
  //   FLAGSWE
  //   IADDRSEL
  //   SELE
  //   SELIFLAGSSEL
  //   MWE
  //   MOE
  //   W16
  //   CRST
  //   IWE
  //   CNZ
endmodule

module IRQCtrl (
  input  nRST,
  input  [5:0] IRQD,
  input  [5:0] IRQMASK,
  input  [5:0] nIRQCLR,
  output IRQR,
  output [5:0] IRQQ
);

  wire n7400_2_pin1, n7408_1_pin3, n7408_1_pin6, n7408_2_pin1, n7408_2_pin6, n7408_2_pin8, n7430_1_pin1,
       n7430_1_pin2, n7430_1_pin3, n7430_1_pin4, n7430_1_pin5, n7430_1_pin6, n7430_1_pin12, n7474_1_pin1,
       n7474_1_pin2, n7474_1_pin13;

  _7430 u_7430_1 (
    .pin1(n7430_1_pin1), .pin2(n7430_1_pin2), .pin3(n7430_1_pin3), .pin4(n7430_1_pin4), .pin5(n7430_1_pin5),
    .pin6(n7430_1_pin6), .pin12(n7430_1_pin12), .pin11(n7430_1_pin12), .pin8(IRQR));  // open: pin13, pin10, pin9
  _7400 u_7400_1 (
    .pin1(IRQMASK[3]), .pin2(IRQQ[3]), .pin3(n7430_1_pin4), .pin4(IRQMASK[2]), .pin5(IRQQ[2]),
    .pin6(n7430_1_pin3), .pin13(IRQMASK[4]), .pin12(IRQQ[4]), .pin11(n7430_1_pin1), .pin10(IRQMASK[5]),
    .pin9(IRQQ[5]), .pin8(n7430_1_pin2));
  _7474 u_7474_1 (
    .pin1(n7474_1_pin1), .pin2(n7474_1_pin2), .pin3(IRQD[4]), .pin4(n7474_1_pin2), .pin5(IRQQ[4]),
    .pin13(n7474_1_pin13), .pin12(n7474_1_pin2), .pin11(IRQD[5]), .pin10(n7474_1_pin2), .pin9(IRQQ[5]));  // open: pin6, pin8
  _7408 u_7408_1 (
    .pin1(nIRQCLR[2]), .pin2(nRST), .pin3(n7408_1_pin3), .pin4(nIRQCLR[3]), .pin5(nRST), .pin6(n7408_1_pin6),
    .pin13(nIRQCLR[4]), .pin12(nRST), .pin11(n7474_1_pin1), .pin10(nIRQCLR[5]), .pin9(nRST),
    .pin8(n7474_1_pin13));
  _7474 u_7474_2 (
    .pin1(n7408_1_pin3), .pin2(n7474_1_pin2), .pin3(IRQD[2]), .pin4(n7474_1_pin2), .pin5(IRQQ[2]),
    .pin13(n7408_1_pin6), .pin12(n7474_1_pin2), .pin11(IRQD[3]), .pin10(n7474_1_pin2), .pin9(IRQQ[3]));  // open: pin6, pin8
  _7408 u_7408_2 (
    .pin1(n7408_2_pin1), .pin2(n7408_2_pin1), .pin4(nIRQCLR[0]), .pin5(nRST), .pin6(n7408_2_pin6),
    .pin13(n7408_2_pin1), .pin12(n7408_2_pin1), .pin10(nRST), .pin9(nIRQCLR[1]), .pin8(n7408_2_pin8));  // open: pin3, pin11
  _7400 u_7400_2 (
    .pin1(n7400_2_pin1), .pin2(n7400_2_pin1), .pin4(n7400_2_pin1), .pin5(n7400_2_pin1), .pin13(IRQMASK[1]),
    .pin12(IRQQ[1]), .pin11(n7430_1_pin5), .pin10(IRQMASK[0]), .pin9(IRQQ[0]), .pin8(n7430_1_pin6));  // open: pin3, pin6
  _7474 u_7474_3 (
    .pin1(n7408_2_pin6), .pin2(n7474_1_pin2), .pin3(IRQD[0]), .pin4(n7474_1_pin2), .pin5(IRQQ[0]),
    .pin13(n7408_2_pin8), .pin12(n7474_1_pin2), .pin11(IRQD[1]), .pin10(n7474_1_pin2), .pin9(IRQQ[1]));  // open: pin6, pin8
  Pull_Resistor pull_resistor_1 (.node(IRQD[3]));
  Pull_Resistor pull_resistor_2 (.node(IRQD[2]));
  Pull_Resistor pull_resistor_3 (.node(IRQD[1]));
  Pull_Resistor pull_resistor_4 (.node(IRQD[0]));
  Pull_Resistor pull_resistor_5 (.node(IRQD[4]));
  Pull_Resistor pull_resistor_6 (.node(IRQD[5]));
  // also tied to GND on the sheet: {n7408_2_pin1, n7400_2_pin1}
  // also tied to VCC on the sheet: {n7430_1_pin12, n7474_1_pin2}
endmodule

module Flags (
  input  CLK,
  input  nWE,
  input  SEL,
  input  CI,
  input  Z,
  input  S,
  input  O,
  input  [15:0] DI,
  input  [5:0] IRQQ,
  output CO,
  output [15:0] DO,
  output [5:0] IRQMASK,
  output [5:0] nIRQCLR
);

  wire [15:0] sel16_1_do;

  Sel16 sel16_1 (.DI0({DO[15:10], nIRQCLR, O, S, Z, CI}), .DI1(DI), .SEL(SEL), .DO(sel16_1_do));
  Reg16 reg16_1 (.CLK(CLK), .nWE(nWE), .D(sel16_1_do), .Q({DO[15:10], nIRQCLR, DO[3:1], CO}));

  assign {DO[9:4], DO[0]} = {IRQQ, CO};
  assign IRQMASK = DO[15:10];
endmodule
module CPU (
  input  CLK,
  input  [15:0] MDI,
  input  [5:0] IRQD,
  input  nRST,
  input  [31:0] DROMD,
  output [21:0] MA,
  output [15:0] MDO,
  output [15:0] DBG_F,
  output DBG_I,
  output [15:0] DBG_PC,
  output [15:0] DBG_R0,
  output [15:0] DBG_R1,
  output [15:0] DBG_R2,
  output [15:0] DBG_R3,
  output [15:0] DBG_R4,
  output [15:0] DBG_R5,
  output [15:0] DBG_R6,
  output [3:0] DBG_CLK,
  output [7:0] DBG_SEL0,
  output [7:0] DBG_SEL1,
  output [7:0] DBG_SEL2,
  output [7:0] DBG_SEL3,
  output [7:0] DBG_SEL4,
  output [7:0] DBG_SEL5,
  output [7:0] DBG_SEL6,
  output [7:0] DBG_SEL7,
  output [8:0] DROMA,
  output MOE,
  output MWE,
  output W16
);

  wire alu_1_co, alu_1_ovf, alu_1_s, alu_1_z, condeval_1_condval, ctrldecoder_1_aluoe, ctrldecoder_1_cnz,
       ctrldecoder_1_crst, ctrldecoder_1_flagsoe, ctrldecoder_1_flagswe, ctrldecoder_1_iaddrsel,
       ctrldecoder_1_iwe, ctrldecoder_1_riwe, ctrldecoder_1_rloe, ctrldecoder_1_rrbusoe, ctrldecoder_1_rroe,
       ctrldecoder_1_sele, flags_1_co, irqctrl_1_irqr, miscintmem_1_q1, n7400_1_pin1, n7400_1_pin4,
       n7400_1_pin8, n7402_1_pin3, n7404_1_pin2, n7404_1_pin4, n7404_1_pin6, n7404_1_pin9, n7404_1_pin10,
       n7404_1_pin12, n7410_1_pin6, n7410_1_pin8, n74161_1_pin3, n74161_1_pin7, n74161_1_pin9;
  wire [0:0] ctrldecoder_1_seliflagssel;
  wire [2:0] alu_1_do, ctrldecoder_1_imm, ctrldecoder_1_ri, ctrldecoder_1_rl, ctrldecoder_1_rr;
  wire [2:2] n7402_1_pin1;
  wire [3:0] conddecoder_1_condcode, ctrldecoder_1_op, sel4_1_do;
  wire [5:0] flags_1_irqmask, flags_1_nirqclr, irqctrl_1_irqq;
  wire [15:0] and16_1_do, immdecoder_1_imm, reg16_1_q, reg16_2_q, regfile_1_ql, regfile_1_qr, sel16_1_do,
       sel16_2_do, sel16_3_do;
  wire [15:3] alu_1_do_2;
  wire [15:14] sel16_4_do;
  wire [15:15] n7400_1_pin6;

  Sel4 sel4_1 (
    .DI0({3'b000, ctrldecoder_1_seliflagssel[0]}), .DI1({{3{DBG_I}}, MDI[0]}), .SEL(ctrldecoder_1_iaddrsel),
    .DO(sel4_1_do));
  _74161 u_74161_1 (
    .pin1(nRST), .pin2(CLK), .pin3(n74161_1_pin3), .pin4(n74161_1_pin3), .pin5(n74161_1_pin3),
    .pin6(n74161_1_pin3), .pin7(n74161_1_pin7), .pin14(DBG_CLK[0]), .pin13(DBG_CLK[1]),
    .pin10(n74161_1_pin7), .pin9(n74161_1_pin9));  // open: pin15, pin12, pin11
  MiscIntMem miscintmem_1 (
    .CLK(CLK), .nCLR(nRST), .D0(sel4_1_do[0]), .WE0(ctrldecoder_1_iwe), .D1(n7410_1_pin8),
    .DEL1(ctrldecoder_1_iaddrsel), .Q0(DBG_I), .Q1(miscintmem_1_q1));
  IRQCtrl irqctrl_1 (
    .nRST(nRST), .IRQD(IRQD), .IRQMASK(flags_1_irqmask), .nIRQCLR(flags_1_nirqclr), .IRQR(irqctrl_1_irqr),
    .IRQQ(irqctrl_1_irqq));
  CtrlDecoder ctrldecoder_1 (
    .DROM(DROMD), .FETCHCYCLE(n7402_1_pin3), .INSTR(reg16_1_q), .OP(ctrldecoder_1_op), .RL(ctrldecoder_1_rl),
    .RLOE(ctrldecoder_1_rloe), .RR(ctrldecoder_1_rr), .RROE(ctrldecoder_1_rroe), .RI(ctrldecoder_1_ri),
    .RIWE(ctrldecoder_1_riwe), .IMM(ctrldecoder_1_imm), .RRBUSOE(ctrldecoder_1_rrbusoe),
    .ALUOE(ctrldecoder_1_aluoe), .FLAGSOE(ctrldecoder_1_flagsoe), .FLAGSWE(ctrldecoder_1_flagswe),
    .IADDRSEL(ctrldecoder_1_iaddrsel), .IWE(ctrldecoder_1_iwe), .SELE(ctrldecoder_1_sele),
    .SELIFLAGSSEL(ctrldecoder_1_seliflagssel[0]), .CNZ(ctrldecoder_1_cnz), .MWE(MWE), .MOE(MOE), .W16(W16),
    .CRST(ctrldecoder_1_crst));
  Sel16 sel16_1 (.DI0(16'h9b3f), .DI1(MDI), .SEL(n7400_1_pin8), .DO(sel16_1_do));
  Reg16 reg16_1 (.CLK(CLK), .nWE(n7404_1_pin6), .D(sel16_1_do), .Q(reg16_1_q));
  CondDecoder conddecoder_1 (.INSTR(reg16_1_q), .CONDCODE(conddecoder_1_condcode));
  ImmDecoder immdecoder_1 (
    .INSTR(reg16_1_q), .SEL(ctrldecoder_1_imm), .nOE(1'b0), .CONDVAL(condeval_1_condval),
    .IMM(immdecoder_1_imm));
  And16 and16_1 (.DI0({16{n7400_1_pin6[15]}}), .DI1(regfile_1_ql), .DO(and16_1_do));
  Sel16 sel16_2 (.DI0(immdecoder_1_imm), .DI1(regfile_1_qr), .SEL(ctrldecoder_1_rroe), .DO(sel16_2_do));
  RegFile regfile_1 (
    .CLK(CLK), .D(MDI), .DSEL(ctrldecoder_1_ri), .WE(ctrldecoder_1_riwe), .QSELL(ctrldecoder_1_rl),
    .OEL(ctrldecoder_1_rloe), .QSELR(ctrldecoder_1_rr), .OER(1'b1), .nPCCLR(nRST), .PCCNTE(n7402_1_pin3),
    .PC0(sel4_1_do[1]), .QL(regfile_1_ql), .QR(regfile_1_qr), .QPC(DBG_PC), .DBG_R0(DBG_R0), .DBG_R1(DBG_R1),
    .DBG_R2(DBG_R2), .DBG_R3(DBG_R3), .DBG_R4(DBG_R4), .DBG_R5(DBG_R5), .DBG_R6(DBG_R6));
  SelRegFile selregfile_1 (
    .CLK(CLK), .D(MDI), .RSEL(alu_1_do), .OWE(ctrldecoder_1_sele), .OnW(ctrldecoder_1_seliflagssel[0]),
    .ASEL({n7402_1_pin1[2], sel16_4_do}), .nCLR(nRST), .Q(MDO), .A(MA[21:14]), .DBG_SEL0(DBG_SEL0),
    .DBG_SEL1(DBG_SEL1), .DBG_SEL2(DBG_SEL2), .DBG_SEL3(DBG_SEL3), .DBG_SEL4(DBG_SEL4), .DBG_SEL5(DBG_SEL5),
    .DBG_SEL6(DBG_SEL6), .DBG_SEL7(DBG_SEL7));
  InstrCompressor instrcompressor_1 (.INSTRI(reg16_1_q), .INSTRO(DROMA[7:0]));
  _7402 u_7402_1 (
    .pin1(n7402_1_pin1[2]), .pin2(miscintmem_1_q1), .pin3(n7402_1_pin3), .pin4(n7402_1_pin3),
    .pin5(DBG_CLK[0]), .pin6(DBG_CLK[1]), .pin13(n74161_1_pin9), .pin12(ctrldecoder_1_crst),
    .pin11(ctrldecoder_1_crst), .pin10(DROMA[8]), .pin9(DBG_CLK[0]), .pin8(DBG_CLK[0]));
  Buf16 buf16_1 (.DI(reg16_2_q), .nOE(ctrldecoder_1_rloe), .DO(regfile_1_ql));
  ALU alu_1 (
    .DIL(and16_1_do), .DIR(sel16_2_do), .OP(ctrldecoder_1_op), .CI(flags_1_co), .DO({alu_1_do_2, alu_1_do}),
    .CO(alu_1_co), .Z(alu_1_z), .S(alu_1_s), .OVF(alu_1_ovf));
  Reg16 reg16_2 (.CLK(CLK), .nWE(1'b0), .D({alu_1_do_2, alu_1_do}), .Q(reg16_2_q));
  Buf16 buf16_2 (.DI({alu_1_do_2, alu_1_do}), .nOE(n7404_1_pin10), .DO(MDO));
  Buf16 buf16_3 (.DI(DBG_F), .nOE(n7404_1_pin2), .DO(MDO));
  _7400 #(.ShowInternalStructure("true")) u_7400_1 (
    .pin1(n7400_1_pin1), .pin2(n7400_1_pin1), .pin4(n7400_1_pin4), .pin5(ctrldecoder_1_cnz),
    .pin6(n7400_1_pin6[15]), .pin13(n7400_1_pin1), .pin12(n7400_1_pin1), .pin10(DBG_I),
    .pin9(irqctrl_1_irqr), .pin8(n7400_1_pin8));  // open: pin3, pin11
  _7404 u_7404_1 (
    .pin1(ctrldecoder_1_flagsoe), .pin2(n7404_1_pin2), .pin3(ctrldecoder_1_rrbusoe), .pin4(n7404_1_pin4),
    .pin5(n7402_1_pin3), .pin6(n7404_1_pin6), .pin13(ctrldecoder_1_flagswe), .pin12(n7404_1_pin12),
    .pin11(ctrldecoder_1_aluoe), .pin10(n7404_1_pin10), .pin9(n7404_1_pin9));  // open: pin8
  Flags flags_1 (
    .CLK(CLK), .nWE(n7404_1_pin12), .SEL(ctrldecoder_1_seliflagssel[0]), .CI(alu_1_co), .Z(alu_1_z),
    .S(alu_1_s), .O(alu_1_ovf), .DI(MDI), .IRQQ(irqctrl_1_irqq), .CO(flags_1_co), .DO(DBG_F),
    .IRQMASK(flags_1_irqmask), .nIRQCLR(flags_1_nirqclr));
  _7410 #(.ShowInternalStructure("true")) u_7410_1 (
    .pin1(ctrldecoder_1_cnz), .pin2(ctrldecoder_1_rloe), .pin3(ctrldecoder_1_rl[2]),
    .pin4(ctrldecoder_1_rl[1]), .pin5(ctrldecoder_1_rl[0]), .pin6(n7410_1_pin6), .pin13(flags_1_co),
    .pin12(n7400_1_pin4), .pin11(n7410_1_pin6), .pin10(n7410_1_pin6), .pin9(n7410_1_pin6), .pin8(n7410_1_pin8));
  Sel16 sel16_3 (.DI0({alu_1_do_2, alu_1_do}), .DI1(reg16_2_q), .SEL(ctrldecoder_1_iaddrsel), .DO(sel16_3_do));
  Sel16 sel16_4 (.DI0(DBG_PC), .DI1(sel16_3_do), .SEL(n7404_1_pin6), .DO({sel16_4_do, MA[13:0]}));
  Buf16 buf16_4 (.DI(regfile_1_qr), .nOE(n7404_1_pin4), .DO(MDO));
  CondEval condeval_1 (
    .C(DBG_F[0]), .Z(DBG_F[1]), .S(DBG_F[2]), .O(DBG_F[3]), .CONDCODE(conddecoder_1_condcode),
    .CONDVAL(condeval_1_condval));

  assign DBG_CLK[3:2] = 2'b00;
  // also tied to GND on the sheet: {n74161_1_pin3, n7404_1_pin9, n7400_1_pin1}
  // also tied to VCC on the sheet: n74161_1_pin7
endmodule
